// Logisim project FlushAndRedirect.circ as structural Verilog: 1 circuit, main circuit main
module main (
  input  IMMtoPC,
  input  RegToPC,
  input  [7:0] NormalPC,
  input  [7:0] JPC,
  output flush,
  output [7:0] NewPC
);

  or or_1 (flush, IMMtoPC, RegToPC);
  Multiplexer #(.width(8), .enable("false")) multiplexer_1 (.in0(NormalPC), .in1(JPC), .out(NewPC), .sel(flush));
endmodule
