// Logisim project RegHazardDetector.circ as structural Verilog: 1 circuit, main circuit main
module main (
  input  [2:0] WriteReg,
  input  RegWrite,
  input  [2:0] ReadReg1,
  input  [2:0] ReadReg2,
  input  ImmToALU,
  input  Clock,
  output Hazard
);

  wire and_1_out, and_2_out, and_3_out, and_4_out, and_5_out, and_6_out, d_ff_1_q, d_ff_2_q, d_ff_3_q,
       d_ff_4_q, d_ff_5_q, d_ff_6_q, d_ff_7_q, d_ff_8_q, d_ff_9_q, d_ff_10_q, d_ff_11_q, d_ff_12_q,
       nor_1_out, nor_2_out, nor_3_out, nor_4_out, nor_5_out, nor_6_out, not_1_out, xor_1_out, xor_2_out,
       xor_3_out, xor_4_out, xor_5_out, xor_6_out, xor_7_out, xor_8_out, xor_9_out, xor_10_out, xor_11_out,
       xor_12_out, xor_13_out, xor_14_out, xor_15_out, xor_16_out, xor_17_out, xor_18_out;

  not not_1 (not_1_out, ImmToALU);
  D_Flip_Flop d_ff_1 (.clk(Clock), .D(WriteReg[0]), .Q(d_ff_1_q), .en(1'b1));  // open: Qn, preset, reset
  D_Flip_Flop d_ff_2 (.clk(Clock), .D(WriteReg[1]), .Q(d_ff_2_q));  // open: Qn, preset, en, reset
  D_Flip_Flop d_ff_3 (.Q(d_ff_3_q), .en(1'b1));  // open: clk, D, Qn, preset, reset
  D_Flip_Flop d_ff_4 (.clk(Clock), .D(RegWrite), .Q(d_ff_4_q), .en(1'b1));  // open: Qn, preset, reset
  xor xor_1 (xor_1_out, d_ff_1_q, ReadReg1[0]);
  xor xor_2 (xor_2_out, d_ff_2_q, ReadReg1[1]);
  xor xor_3 (xor_3_out, d_ff_3_q, ReadReg1[2]);
  xor xor_4 (xor_4_out, d_ff_1_q, ReadReg2[0]);
  xor xor_5 (xor_5_out, d_ff_2_q, ReadReg2[1]);
  xor xor_6 (xor_6_out, d_ff_3_q, ReadReg2[2]);
  D_Flip_Flop d_ff_5 (.clk(Clock), .D(d_ff_1_q), .Q(d_ff_5_q), .en(1'b1));  // open: Qn, preset, reset
  D_Flip_Flop d_ff_6 (.clk(Clock), .D(d_ff_2_q), .Q(d_ff_6_q), .en(1'b1));  // open: Qn, preset, reset
  D_Flip_Flop d_ff_7 (.clk(Clock), .D(d_ff_3_q), .Q(d_ff_7_q), .en(1'b1));  // open: Qn, preset, reset
  D_Flip_Flop d_ff_8 (.clk(Clock), .D(d_ff_4_q), .Q(d_ff_8_q), .en(1'b1));  // open: Qn, preset, reset
  and and_1 (and_1_out, d_ff_4_q, nor_1_out);
  nor nor_1 (nor_1_out, xor_1_out, xor_2_out, xor_3_out);
  and and_2 (and_2_out, d_ff_4_q, not_1_out, nor_2_out);
  nor nor_2 (nor_2_out, xor_4_out, xor_5_out, xor_6_out);
  xor xor_7 (xor_7_out, d_ff_5_q, ReadReg1[0]);
  xor xor_8 (xor_8_out, d_ff_6_q, ReadReg1[1]);
  xor xor_9 (xor_9_out, d_ff_7_q, ReadReg1[2]);
  xor xor_10 (xor_10_out, d_ff_5_q, ReadReg2[0]);
  xor xor_11 (xor_11_out, d_ff_6_q, ReadReg2[1]);
  xor xor_12 (xor_12_out, d_ff_7_q, ReadReg2[2]);
  D_Flip_Flop d_ff_9 (.clk(Clock), .D(d_ff_5_q), .Q(d_ff_9_q), .en(1'b1));  // open: Qn, preset, reset
  D_Flip_Flop d_ff_10 (.clk(Clock), .D(d_ff_6_q), .Q(d_ff_10_q), .en(1'b1));  // open: Qn, preset, reset
  D_Flip_Flop d_ff_11 (.clk(Clock), .D(d_ff_7_q), .Q(d_ff_11_q), .en(1'b1));  // open: Qn, preset, reset
  D_Flip_Flop d_ff_12 (.clk(Clock), .D(d_ff_8_q), .Q(d_ff_12_q), .en(1'b1));  // open: Qn, preset, reset
  and and_3 (and_3_out, d_ff_8_q, nor_3_out);
  nor nor_3 (nor_3_out, xor_7_out, xor_8_out, xor_9_out);
  and and_4 (and_4_out, d_ff_8_q, not_1_out, nor_4_out);
  nor nor_4 (nor_4_out, xor_10_out, xor_11_out, xor_12_out);
  xor xor_13 (xor_13_out, d_ff_9_q, ReadReg2[0]);
  xor xor_14 (xor_14_out, d_ff_10_q, ReadReg2[1]);
  xor xor_15 (xor_15_out, d_ff_11_q, ReadReg2[2]);
  xor xor_16 (xor_16_out, d_ff_9_q, ReadReg1[0]);
  nor nor_5 (nor_5_out, xor_16_out, xor_17_out, xor_18_out);
  xor xor_17 (xor_17_out, d_ff_11_q, ReadReg1[1]);
  xor xor_18 (xor_18_out, d_ff_10_q, ReadReg1[2]);
  nor nor_6 (nor_6_out, xor_13_out, xor_14_out, xor_15_out);
  and and_5 (and_5_out, d_ff_12_q, nor_5_out);
  and and_6 (and_6_out, d_ff_12_q, nor_6_out, not_1_out);
  or or_1 (Hazard, and_5_out, and_3_out, and_1_out, and_6_out, and_4_out, and_2_out);
endmodule
