// Logisim project coemipsPipeLinedLAD.circ as structural Verilog: 28 circuits, main circuit main
module main (
);

  wire ALU_zero, and_1_out, bubblegen_1_out_2, clock_1_out, Decoder_halt, Decoder_immtoalu, Decoder_immtopc,
       Decoder_led, Decoder_memread, Decoder_memtoreg, Decoder_memwrite, Decoder_pctoreg, Decoder_regtopc,
       Decoder_regwrite, Decoder_shiftertoreg, Decoder_shiftsrc, Decoder_writeled, Decoder_zerostoalu,
       ex_mem_1_led_2, ex_mem_1_memread_2, ex_mem_1_memtoreg_2, ex_mem_1_memwrite_2, ex_mem_1_pctoreg_2,
       ex_mem_1_regwrite_2, ex_mem_1_shiftertoreg_2, ex_mem_1_writeled_2, Flush_detector_flush,
       forwardunit_1__1fromalu, forwardunit_1__1frommem, forwardunit_1__2fromalu, forwardunit_1__2frommem,
       forwardunit_1_reg1toggle, forwardunit_1_reg2toggle, id_ex_1_immtoalu_2, id_ex_1_led_2,
       id_ex_1_memread_2, id_ex_1_memtoreg_2, id_ex_1_memwrite_2, id_ex_1_pctoreg_2, id_ex_1_regwrite_2,
       id_ex_1_shiftertoreg_2, id_ex_1_shiftsrc_2, id_ex_1_subop_3, id_ex_1_writeled_2, id_ex_1_zerostoalu_2,
       Instruction_Splitter_subop, Instruction_Splitter_unsigned, mem_wb_1_led_2, mem_wb_1_memtoreg_2,
       mem_wb_1_pctoreg_2, mem_wb_1_regwrite_2, mem_wb_1_shiftertoreg_2, mem_wb_1_writeled_2,
       MemForward_aluselect1, MemForward_aluselect2, MemForward_regselect1, MemForward_regselect2, not_1_out,
       not_2_out, or_1_out, Reset_out, ResultToLess_less;
  wire [2:0] ex_mem_1_writereg_2, id_ex_1_out_34, Instruction_Splitter_readregister1,
       Instruction_Splitter_readregister2, Instruction_Splitter_writeregister, mem_wb_1_writereg_2,
       multiplexer_1_out, register_2_q;
  wire [3:0] Decoder_aluop, id_ex_1_aluop_2, id_ex_1_shiftamount_2, Instruction_Splitter_opcode,
       Instruction_Splitter_shiftamount;
  wire [7:0] adder_1_out, ex_mem_1_address_2, Flush_detector_newpc, id_ex_1_pc_4_2, if_id_1_pc_4_2,
       Instruction_Splitter_immediate, multiplexer_2_out, multiplexer_5_out, PC_q, register_1_q,
       RegistertoAddress_2_address, RegistertoAddress_address;
  wire [15:0] ALU_result, bit_extender_1_out, ex_mem_1_pc_4ext_2, ex_mem_1_read_data_1_2, ex_mem_1_result_2,
       ex_mem_1_shiftout_2, id_ex_1_imm_2, id_ex_1_read_data_1_2, id_ex_1_read_data_2_2,
       if_id_1_instructions, mem_wb_1_d_2, mem_wb_1_pc_4ext_2, mem_wb_1_readdata1_2, mem_wb_1_result_2,
       mem_wb_1_shiftout_2, multiplexer_3_out, multiplexer_4_out, multiplexer_6_out, multiplexer_7_out,
       multiplexer_8_out, multiplexer_9_out, multiplexer_10_out, multiplexer_11_out, multiplexer_12_out,
       multiplexer_13_out, multiplexer_14_out, multiplexer_15_out, multiplexer_16_out, multiplexer_17_out,
       multiplexer_18_out, multiplexer_19_out, multiplexer_20_out, multiplexer_21_out, ram_1_data,
       register_3_q, Registers_readdata1, Registers_readdata2, rom_1_data, Shifter_shiftout,
       Sign_Extend_signextendedimm;

  Clock clock_1 (.out(clock_1_out));
  Register PC (.D(Flush_detector_newpc), .en(not_1_out), .Q(PC_q), .clk(and_1_out), .clr(Reset_out));
  not not_1 (not_1_out, Decoder_halt);
  Button Reset (.out(Reset_out));
  and and_1 (and_1_out, clock_1_out, not_2_out);
  not not_2 (not_2_out, bubblegen_1_out_2);
  Adder adder_1 (.a(PC_q), .b(8'h1), .out(adder_1_out));  // open: cin, cout
  ROM #(.dataWidth(16)) rom_1 (.addr(PC_q), .data(rom_1_data), .sel(1'b1));
  or or_1 (or_1_out, bubblegen_1_out_2, Flush_detector_flush);
  InstructionSplitter Instruction_Splitter (
    .Instruction(if_id_1_instructions), .Opcode(Instruction_Splitter_opcode),
    .ReadRegister1(Instruction_Splitter_readregister1), .ReadRegister2(Instruction_Splitter_readregister2),
    .WriteRegister(Instruction_Splitter_writeregister), .ShiftAmount(Instruction_Splitter_shiftamount),
    .SubOp(Instruction_Splitter_subop), .Unsigned(Instruction_Splitter_unsigned),
    .Immediate(Instruction_Splitter_immediate));
  IF_ID if_id_1 (
    .PC_4(adder_1_out), .Instruction(rom_1_data), .CLK(clock_1_out), .PC_4_2(if_id_1_pc_4_2),
    .Instructions(if_id_1_instructions), .Enable(Decoder_halt), .Flush(or_1_out));
  Register register_1 (
    .D(Instruction_Splitter_immediate), .en(1'b1), .Q(register_1_q), .clk(clock_1_out));  // open: clr
  ALUtoPC RegistertoAddress (.ALUOut(multiplexer_6_out), .Address(RegistertoAddress_address));
  Multiplexer #(.width(3), .enable("false")) multiplexer_1 (
    .in0(Instruction_Splitter_readregister1), .in1(register_2_q), .out(multiplexer_1_out),
    .sel(Decoder_regtopc));
  Register #(.width(3)) register_2 (
    .D(Instruction_Splitter_readregister1), .en(1'b1), .Q(register_2_q), .clk(clock_1_out));  // open: clr
  BubbleGen bubblegen_1 (.Opcode(Instruction_Splitter_opcode), .out_2(bubblegen_1_out_2));
  ResultToLess ResultToLess (.Result(ALU_result), .Less(ResultToLess_less));
  SignExtend Sign_Extend (
    .Unsigned(Instruction_Splitter_unsigned), .Immediate(Instruction_Splitter_immediate),
    .SignExtendedImm(Sign_Extend_signextendedimm));
  Decoder Decoder (
    .Opcode(Instruction_Splitter_opcode), .Subop(Instruction_Splitter_subop), .Zero(ALU_zero),
    .Less(ResultToLess_less), .Clock(clock_1_out), .ShiftSrc(Decoder_shiftsrc),
    .ShifterToReg(Decoder_shiftertoreg), .RegWrite(Decoder_regwrite), .ALUOp(Decoder_aluop),
    .IMMtoALU(Decoder_immtoalu), .RegtoPC(Decoder_regtopc), .IMMtoPC(Decoder_immtopc),
    .ZerosToALU(Decoder_zerostoalu), .MemWrite(Decoder_memwrite), .MemtoReg(Decoder_memtoreg),
    .Halt(Decoder_halt), .LED(Decoder_led), .WriteLED(Decoder_writeled), .MemRead(Decoder_memread),
    .PCtoReg(Decoder_pctoreg));
  RegisterFile Registers (
    .ReadRegister1(multiplexer_1_out), .ReadRegister2(Instruction_Splitter_readregister2),
    .WriteRegister(mem_wb_1_writereg_2), .WriteData(multiplexer_19_out), .WriteEnable(mem_wb_1_regwrite_2),
    .Clock(clock_1_out), .ReadData1(Registers_readdata1), .ReadData2(Registers_readdata2));
  Multiplexer #(.width(8), .disabled(0), .enable("false")) multiplexer_2 (
    .in0(adder_1_out), .in1(register_1_q), .out(multiplexer_2_out), .sel(Decoder_immtopc));
  Multiplexer #(.width(16), .enable("false")) multiplexer_3 (
    .in0(Registers_readdata1), .in1(multiplexer_13_out), .out(multiplexer_3_out),
    .sel(forwardunit_1_reg1toggle));
  Multiplexer #(.width(16), .enable("false")) multiplexer_4 (
    .in0(Registers_readdata2), .in1(multiplexer_12_out), .out(multiplexer_4_out),
    .sel(forwardunit_1_reg2toggle));
  Multiplexer #(.width(8), .disabled(0), .enable("false")) multiplexer_5 (
    .in0(multiplexer_2_out), .in1(RegistertoAddress_address), .out(multiplexer_5_out), .sel(Decoder_regtopc));
  Multiplexer #(.width(16), .enable("false")) multiplexer_6 (
    .in0(multiplexer_3_out), .in1(ram_1_data), .out(multiplexer_6_out), .sel(MemForward_regselect1));
  Multiplexer #(.width(16), .enable("false")) multiplexer_7 (
    .in0(multiplexer_4_out), .in1(ram_1_data), .out(multiplexer_7_out), .sel(MemForward_regselect2));
  ID_EX id_ex_1 (
    .Read_Data_1(multiplexer_6_out), .Read_Data_2(multiplexer_7_out), .IMM(Sign_Extend_signextendedimm),
    .ShiftSrc(Decoder_shiftsrc), .ShifterToReg(Decoder_shiftertoreg), .RegWrite(Decoder_regwrite),
    .ALUOp(Decoder_aluop), .IMMtoALU(Decoder_immtoalu), .ZerosToALU(Decoder_zerostoalu),
    .MemWrite(Decoder_memwrite), .MemToReg(Decoder_memtoreg), .LED(Decoder_led), .MemRead(Decoder_memread),
    .PCtoReg(Decoder_pctoreg), .Read_Data_1_2(id_ex_1_read_data_1_2), .Read_Data_2_2(id_ex_1_read_data_2_2),
    .IMM_2(id_ex_1_imm_2), .ShiftSrc_2(id_ex_1_shiftsrc_2), .ShifterToReg_2(id_ex_1_shiftertoreg_2),
    .RegWrite_2(id_ex_1_regwrite_2), .ALUOp_2(id_ex_1_aluop_2), .IMMtoALU_2(id_ex_1_immtoalu_2),
    .MemWrite_2(id_ex_1_memwrite_2), .MemToReg_2(id_ex_1_memtoreg_2), .LED_2(id_ex_1_led_2),
    .MemRead_2(id_ex_1_memread_2), .PCtoReg_2(id_ex_1_pctoreg_2), .Clock(clock_1_out),
    .WriteLED(Decoder_writeled), .WriteLED_2(id_ex_1_writeled_2), .SubOP(Instruction_Splitter_subop),
    .ShiftAmount(Instruction_Splitter_shiftamount), .PC_4(if_id_1_pc_4_2), .SubOP_3(id_ex_1_subop_3),
    .ShiftAmount_2(id_ex_1_shiftamount_2), .PC_4_2(id_ex_1_pc_4_2), .ZerostoALU_2(id_ex_1_zerostoalu_2),
    .SubOp_2(Instruction_Splitter_subop), .WriteReg(Instruction_Splitter_writeregister),
    .out_34(id_ex_1_out_34));  // open: SubOp_4, clear
  FlushDetector Flush_detector (
    .IMMtoPC(Decoder_immtopc), .RegToPC(Decoder_regtopc), .NormalPC(adder_1_out), .JPC(multiplexer_5_out),
    .flush(Flush_detector_flush), .NewPC(Flush_detector_newpc));
  Multiplexer #(.width(16), .disabled(0), .enable("false")) multiplexer_8 (
    .in0(id_ex_1_read_data_2_2), .in1(id_ex_1_imm_2), .out(multiplexer_8_out), .sel(id_ex_1_immtoalu_2));
  Multiplexer #(.width(16), .disabled(0), .enable("false")) multiplexer_9 (
    .in0(multiplexer_8_out), .in1({16{1'b0}}), .out(multiplexer_9_out), .sel(id_ex_1_zerostoalu_2));
  Shifter Shifter (
    .Subop(id_ex_1_subop_3), .Data(multiplexer_10_out), .ShamtReg(multiplexer_11_out),
    .ShiftSrc(id_ex_1_shiftsrc_2), .Shamt(id_ex_1_shiftamount_2), .ShiftOut(Shifter_shiftout));
  Multiplexer #(.width(16), .enable("false")) multiplexer_10 (
    .in0(id_ex_1_read_data_1_2), .in1(ram_1_data), .out(multiplexer_10_out), .sel(MemForward_aluselect1));
  assign bit_extender_1_out = {{8{1'b0}}, id_ex_1_pc_4_2};  // Bit_Extender bit_extender_1
  ForwardUnit forwardunit_1 (
    .WriteReg(Instruction_Splitter_writeregister), .RegWrite(Decoder_regwrite), .ReadReg1(multiplexer_1_out),
    .ReadReg2(Instruction_Splitter_readregister2), .ImmToALU(Decoder_immtoalu), .Clock(clock_1_out),
    ._1FromALU(forwardunit_1__1fromalu), ._2FromALU(forwardunit_1__2fromalu),
    ._1FromMem(forwardunit_1__1frommem), ._2FromMem(forwardunit_1__2frommem),
    .Reg1Toggle(forwardunit_1_reg1toggle), .Reg2Toggle(forwardunit_1_reg2toggle));  // open: _1FromWB, _2FromWB, Hazard
  Multiplexer #(.width(16), .enable("false")) multiplexer_11 (
    .in0(multiplexer_9_out), .in1(ram_1_data), .out(multiplexer_11_out), .sel(MemForward_aluselect2));
  Multiplexer #(.width(16), .enable("false")) multiplexer_12 (
    .in0(multiplexer_14_out), .in1(ALU_result), .out(multiplexer_12_out), .sel(forwardunit_1__2fromalu));
  Multiplexer #(.width(16), .enable("false")) multiplexer_13 (
    .in0(multiplexer_15_out), .in1(ALU_result), .out(multiplexer_13_out), .sel(forwardunit_1__1fromalu));
  sixteen_bit_ALU ALU (
    .ALUOperation(id_ex_1_aluop_2), .a(multiplexer_10_out), .b(multiplexer_11_out), .Zero(ALU_zero),
    .Result(ALU_result));  // open: Overflow
  ALUtoPC RegistertoAddress_2 (.ALUOut(multiplexer_11_out), .Address(RegistertoAddress_2_address));
  Multiplexer #(.width(16), .enable("false")) multiplexer_14 (
    .in0(multiplexer_19_out), .in1(multiplexer_16_out), .out(multiplexer_14_out),
    .sel(forwardunit_1__2frommem));
  Multiplexer #(.width(16), .enable("false")) multiplexer_15 (
    .in0(multiplexer_19_out), .in1(multiplexer_16_out), .out(multiplexer_15_out),
    .sel(forwardunit_1__1frommem));
  EX_MEM ex_mem_1 (
    .Read_Data_1(multiplexer_10_out), .Read_Data_1_2(ex_mem_1_read_data_1_2), .ShiftOut(Shifter_shiftout),
    .ShiftOut_2(ex_mem_1_shiftout_2), .Result(ALU_result), .Result_2(ex_mem_1_result_2),
    .PC_4EXT(bit_extender_1_out), .PC_4EXT_2(ex_mem_1_pc_4ext_2), .ShifterToReg(id_ex_1_shiftertoreg_2),
    .ShifterToReg_2(ex_mem_1_shiftertoreg_2), .RegWrite(id_ex_1_regwrite_2),
    .RegWrite_2(ex_mem_1_regwrite_2), .MemWrite(id_ex_1_memwrite_2), .MemWrite_2(ex_mem_1_memwrite_2),
    .MemToReg(id_ex_1_memtoreg_2), .MemToReg_2(ex_mem_1_memtoreg_2), .LED(id_ex_1_led_2),
    .LED_2(ex_mem_1_led_2), .WriteLED(id_ex_1_writeled_2), .WriteLED_2(ex_mem_1_writeled_2),
    .MemRead(id_ex_1_memread_2), .MemRead_2(ex_mem_1_memread_2), .PCtoReg(id_ex_1_pctoreg_2),
    .PCtoReg_2(ex_mem_1_pctoreg_2), .Clock(clock_1_out), .Address(RegistertoAddress_2_address),
    .Address_2(ex_mem_1_address_2), .WriteReg(id_ex_1_out_34), .WriteReg_2(ex_mem_1_writereg_2));  // open: ShiftAmount, ShiftAmount_2, SubOP, SubOP_2, ShiftSrc, ShiftSrc_2, Halt, Halt_2
  Multiplexer #(.width(16), .enable("false")) multiplexer_16 (
    .in0(multiplexer_17_out), .in1(ex_mem_1_pc_4ext_2), .out(multiplexer_16_out), .sel(ex_mem_1_pctoreg_2));
  Multiplexer #(.width(16), .enable("false")) multiplexer_17 (
    .in0(multiplexer_18_out), .in1(ex_mem_1_shiftout_2), .out(multiplexer_17_out),
    .sel(ex_mem_1_shiftertoreg_2));
  Multiplexer #(.width(16), .enable("false")) multiplexer_18 (
    .in0(ex_mem_1_result_2), .in1(ram_1_data), .out(multiplexer_18_out), .sel(ex_mem_1_memtoreg_2));
  MemForward MemForward (
    .memReg(ex_mem_1_writereg_2), .nextReg1(multiplexer_1_out),
    .nextReg2(Instruction_Splitter_readregister2), .MemRead(ex_mem_1_memread_2),
    .ALUSelect1(MemForward_aluselect1), .ALUSelect2(MemForward_aluselect2), .clk(clock_1_out),
    .regSelect1(MemForward_regselect1), .regSelect2(MemForward_regselect2));
  RAM #(.dataWidth(16), .bus("separate")) ram_1 (
    .addr(ex_mem_1_address_2), .din(ex_mem_1_read_data_1_2), .data(ram_1_data), .str(ex_mem_1_memwrite_2),
    .sel(1'b1), .clk(clock_1_out), .ld(ex_mem_1_memread_2));  // open: clr
  MEM_WB mem_wb_1 (
    .D(ram_1_data), .Result(ex_mem_1_result_2), .ShifterToReg(ex_mem_1_shiftertoreg_2),
    .ReadData1(ex_mem_1_read_data_1_2), .ShiftOut(ex_mem_1_shiftout_2), .PC_4EXT(ex_mem_1_pc_4ext_2),
    .RegWrite(ex_mem_1_regwrite_2), .MemToReg(ex_mem_1_memtoreg_2), .LED(ex_mem_1_led_2),
    .WriteLED(ex_mem_1_writeled_2), .PCtoReg(ex_mem_1_pctoreg_2), .D_2(mem_wb_1_d_2),
    .Result_2(mem_wb_1_result_2), .ShifterToReg_2(mem_wb_1_shiftertoreg_2),
    .ReadData1_2(mem_wb_1_readdata1_2), .ShiftOut_2(mem_wb_1_shiftout_2), .PC_4EXT_2(mem_wb_1_pc_4ext_2),
    .RegWrite_2(mem_wb_1_regwrite_2), .MemToReg_2(mem_wb_1_memtoreg_2), .LED_2(mem_wb_1_led_2),
    .WriteLED_2(mem_wb_1_writeled_2), .PCtoReg_2(mem_wb_1_pctoreg_2), .in_17(clock_1_out),
    .WriteReg(ex_mem_1_writereg_2), .WriteReg_2(mem_wb_1_writereg_2));  // open: SubOP, Shiftsrc, ShiftAmount, SubOP_2, ShiftSrc_2, ShiftAmount_2, Halt, Halt_2
  Multiplexer #(.width(16), .disabled(0), .enable("false")) multiplexer_19 (
    .in0(multiplexer_21_out), .in1(mem_wb_1_pc_4ext_2), .out(multiplexer_19_out), .sel(mem_wb_1_pctoreg_2));
  Multiplexer #(.width(16), .enable("false")) multiplexer_20 (
    .in0(mem_wb_1_result_2), .in1(mem_wb_1_d_2), .out(multiplexer_20_out), .sel(mem_wb_1_memtoreg_2));
  Multiplexer #(.width(16), .disabled(0), .enable("false")) multiplexer_21 (
    .in0(multiplexer_20_out), .in1(mem_wb_1_shiftout_2), .out(multiplexer_21_out),
    .sel(mem_wb_1_shiftertoreg_2));
  Hex_Digit_Display hex_digit_display_1 (.value(register_3_q[15:12]));  // open: dp
  Register #(.width(16)) register_3 (
    .D(mem_wb_1_readdata1_2), .en(mem_wb_1_writeled_2), .Q(register_3_q), .clk(clock_1_out));  // open: clr
  LED Halt (.in(mem_wb_1_led_2));
  Hex_Digit_Display hex_digit_display_2 (.value(register_3_q[7:4]));  // open: dp
  Hex_Digit_Display hex_digit_display_3 (.value(register_3_q[11:8]));  // open: dp
  Hex_Digit_Display hex_digit_display_4 (.value(register_3_q[3:0]));  // open: dp

  // Notes on the sheet:
  //   contents of rom_1 (hex, n*v repeats v):
  //   1202 1404 180a 1c01 1e04 4*0 280 8603 280 6f00 280 b80 1000 1000 1000 f200 f800
endmodule

module InstructionSplitter (
  input  [15:0] Instruction,
  output [3:0] Opcode,
  output [2:0] ReadRegister1,
  output [2:0] ReadRegister2,
  output [2:0] WriteRegister,
  output [3:0] ShiftAmount,
  output SubOp,
  output Unsigned,
  output [7:0] Immediate
);


  assign Immediate = Instruction[7:0];
  assign Opcode = Instruction[15:12];
  assign ReadRegister1 = Instruction[11:9];
  assign ReadRegister2 = Instruction[8:6];
  assign ShiftAmount = Instruction[4:1];
  assign SubOp = Instruction[0];
  assign Unsigned = Instruction[8];
  assign WriteRegister = Instruction[11:9];
endmodule

module SignExtend (
  input  Unsigned,
  input  [7:0] Immediate,
  output [15:0] SignExtendedImm
);

  wire [15:0] bit_extender_1_out, bit_extender_2_out;

  assign bit_extender_1_out = {{8{Immediate[7]}}, Immediate};  // Bit_Extender bit_extender_1
  assign bit_extender_2_out = {{8{1'b0}}, Immediate};  // Bit_Extender bit_extender_2
  Multiplexer #(.width(16), .disabled(0), .enable("false")) multiplexer_1 (
    .in0(bit_extender_1_out), .in1(bit_extender_2_out), .out(SignExtendedImm), .sel(Unsigned));
endmodule

module ALUtoPC (
  input  [15:0] ALUOut,
  output [7:0] Address
);


  assign Address = ALUOut[7:0];
endmodule

module Shifter (
  input  Subop,
  input  [15:0] Data,
  input  [15:0] ShamtReg,
  input  ShiftSrc,
  input  [3:0] Shamt,
  output [15:0] ShiftOut
);

  wire [3:0] multiplexer_1_out;
  wire [15:0] shifter_1_out, shifter_2_out;

  Multiplexer #(.width(4), .disabled(0), .enable("false")) multiplexer_1 (
    .in0(ShamtReg[3:0]), .in1(Shamt), .out(multiplexer_1_out), .sel(ShiftSrc));
  Shifter_part #(.width(16)) shifter_1 (.in(Data), .\dist (multiplexer_1_out), .out(shifter_1_out));
  Shifter_part #(.width(16), .shift("lr")) shifter_2 (.in(Data), .\dist (multiplexer_1_out), .out(shifter_2_out));
  Multiplexer #(.width(16), .disabled(0), .enable("false")) multiplexer_2 (
    .in0(shifter_1_out), .in1(shifter_2_out), .out(ShiftOut), .sel(Subop));
endmodule

module RegisterFile (
  input  [2:0] ReadRegister1,
  input  [2:0] ReadRegister2,
  input  [2:0] WriteRegister,
  input  [15:0] WriteData,
  input  WriteEnable,
  input  Clock,
  output [15:0] ReadData1,
  output [15:0] ReadData2
);

  wire decoder_1_out0, decoder_1_out1, decoder_1_out2, decoder_1_out3, decoder_1_out4, decoder_1_out5,
       decoder_1_out6, decoder_1_out7;
  wire [15:0] register_1_q, register_2_q, register_3_q, register_4_q, register_5_q, register_6_q,
       register_7_q, register_8_q;

  Decoder_part #(.select(3), .disabled(0)) decoder_1 (
    .out0(decoder_1_out0), .out1(decoder_1_out1), .out2(decoder_1_out2), .out3(decoder_1_out3),
    .out4(decoder_1_out4), .out5(decoder_1_out5), .out6(decoder_1_out6), .out7(decoder_1_out7),
    .sel(WriteRegister), .en(WriteEnable));
  Register #(.width(16)) register_1 (.D(WriteData), .en(decoder_1_out0), .Q(register_1_q), .clk(Clock));  // open: clr
  Register #(.width(16)) register_2 (.D(WriteData), .en(decoder_1_out1), .Q(register_2_q), .clk(Clock));  // open: clr
  Register #(.width(16)) register_3 (.D(WriteData), .en(decoder_1_out2), .Q(register_3_q), .clk(Clock));  // open: clr
  Register #(.width(16)) register_4 (.D(WriteData), .en(decoder_1_out3), .Q(register_4_q), .clk(Clock));  // open: clr
  Register #(.width(16)) register_5 (.D(WriteData), .en(decoder_1_out4), .Q(register_5_q), .clk(Clock));  // open: clr
  Register #(.width(16)) register_6 (.D(WriteData), .en(decoder_1_out5), .Q(register_6_q), .clk(Clock));  // open: clr
  Register #(.width(16)) register_7 (.D(WriteData), .en(decoder_1_out6), .Q(register_7_q), .clk(Clock));  // open: clr
  Register #(.width(16)) register_8 (.D(WriteData), .en(decoder_1_out7), .Q(register_8_q), .clk(Clock));  // open: clr
  Multiplexer #(.select(3), .width(16), .enable("false")) multiplexer_1 (
    .in0(register_1_q), .in1(register_2_q), .in2(register_3_q), .in3(register_4_q), .in4(register_5_q),
    .in5(register_6_q), .in6(register_7_q), .in7(register_8_q), .out(ReadData1), .sel(ReadRegister1));
  Multiplexer #(.select(3), .width(16), .enable("false")) multiplexer_2 (
    .in0(register_1_q), .in1(register_2_q), .in2(register_3_q), .in3(register_4_q), .in4(register_5_q),
    .in5(register_6_q), .in6(register_7_q), .in7(register_8_q), .out(ReadData2), .sel(ReadRegister2));
endmodule

module ShifterDecoder (
  input  [3:0] Opcode,
  output ShiftSrc,
  output ShiftertoReg,
  output RegWrite
);

  and and_1 (RegWrite, ~Opcode[3], Opcode[2], ~Opcode[1]);  // AND_Gate

  assign ShiftertoReg = RegWrite;
  assign ShiftSrc = Opcode[0];
endmodule

module Arith_Log_Decoder (
  input  [3:0] Opcode,
  input  Subop,
  output [3:0] ALUOperation,
  output RegWrite,
  output ALUSrc
);

  wire and_2_out, and_3_out, and_5_out, and_6_out, not_1_out, not_2_out, not_3_out, not_4_out, not_5_out,
       not_6_out, not_7_out, not_8_out, not_9_out, not_10_out, not_11_out, not_12_out, not_13_out,
       not_14_out, not_15_out, not_16_out, not_17_out, not_18_out, not_19_out, not_20_out, not_21_out;

  not not_1 (not_1_out, Opcode[3]);
  not not_2 (not_2_out, Opcode[2]);
  not not_3 (not_3_out, Subop);
  not not_4 (not_4_out, Opcode[3]);
  not not_5 (not_5_out, Opcode[2]);
  not not_6 (not_6_out, Opcode[1]);
  not not_7 (not_7_out, Opcode[0]);
  not not_8 (not_8_out, Opcode[3]);
  not not_9 (not_9_out, Opcode[2]);
  not not_10 (not_10_out, Subop);
  not not_11 (not_11_out, Opcode[3]);
  not not_12 (not_12_out, Opcode[2]);
  not not_13 (not_13_out, Opcode[1]);
  not not_14 (not_14_out, Opcode[3]);
  not not_15 (not_15_out, Opcode[2]);
  not not_16 (not_16_out, Opcode[1]);
  not not_17 (not_17_out, Opcode[3]);
  not not_18 (not_18_out, Opcode[2]);
  not not_19 (not_19_out, Opcode[3]);
  not not_20 (not_20_out, Opcode[2]);
  not not_21 (not_21_out, Opcode[1]);
  and and_1 (ALUOperation[3], not_1_out, not_2_out, Opcode[1], Opcode[0], not_3_out);
  and and_2 (and_2_out, not_4_out, not_5_out, not_6_out, not_7_out, Subop);
  and and_3 (and_3_out, not_8_out, not_9_out, Opcode[1], Opcode[0], not_10_out);
  and and_4 (ALUOperation[1], not_11_out, not_12_out, not_13_out);
  and and_5 (and_5_out, not_14_out, not_15_out, not_16_out);
  and and_6 (and_6_out, not_17_out, not_18_out, Opcode[0]);
  and and_7 (ALUSrc, not_19_out, not_20_out, not_21_out, Opcode[0]);
  or or_1 (ALUOperation[2], and_2_out, and_3_out);
  or or_2 (RegWrite, and_5_out, and_6_out);

  assign ALUOperation[0] = 1'b0;
endmodule

module Arith_Log (
  input  Opcode3,
  input  Opcode2,
  input  Opcode1,
  input  Opcode0,
  input  Unsigned,
  input  Subop,
  output ALUOp3,
  output ALUOp2,
  output ALUOp1,
  output ALUOp0,
  output RegWrite,
  output ALUSrc
);

  wire and_2_out, and_3_out, and_5_out, and_6_out, not_1_out, not_2_out, not_3_out, not_4_out, not_5_out,
       not_6_out, not_7_out, not_8_out, not_9_out, not_10_out, not_11_out, not_12_out, not_13_out,
       not_14_out, not_15_out, not_16_out, not_17_out, not_18_out, not_19_out, not_20_out, not_21_out;

  not not_1 (not_1_out, Opcode3);
  not not_2 (not_2_out, Opcode2);
  not not_3 (not_3_out, Subop);
  not not_4 (not_4_out, Opcode3);
  not not_5 (not_5_out, Opcode2);
  not not_6 (not_6_out, Opcode1);
  not not_7 (not_7_out, Opcode0);
  not not_8 (not_8_out, Opcode3);
  not not_9 (not_9_out, Opcode2);
  not not_10 (not_10_out, Subop);
  not not_11 (not_11_out, Opcode3);
  not not_12 (not_12_out, Opcode2);
  not not_13 (not_13_out, Opcode1);
  not not_14 (not_14_out, Opcode3);
  not not_15 (not_15_out, Opcode2);
  not not_16 (not_16_out, Opcode1);
  not not_17 (not_17_out, Opcode3);
  not not_18 (not_18_out, Opcode2);
  not not_19 (not_19_out, Opcode3);
  not not_20 (not_20_out, Opcode2);
  not not_21 (not_21_out, Opcode1);
  and and_1 (ALUOp3, not_1_out, not_2_out, Opcode1, Opcode0, not_3_out);
  and and_2 (and_2_out, not_4_out, not_5_out, not_6_out, not_7_out, Subop);
  and and_3 (and_3_out, not_8_out, not_9_out, Opcode1, Opcode0, not_10_out);
  and and_4 (ALUOp1, not_11_out, not_12_out, not_13_out);
  and and_5 (and_5_out, not_14_out, not_15_out, not_16_out);
  and and_6 (and_6_out, not_17_out, not_18_out, Opcode0);
  and and_7 (ALUSrc, not_19_out, not_20_out, not_21_out, Opcode0);
  or or_1 (ALUOp2, and_2_out, and_3_out);
  or or_2 (RegWrite, and_5_out, and_6_out);

  assign ALUOp0 = 1'b0;
endmodule

module one_bit_ALU (
  input  Ainvert,
  input  Binvert,
  input  CarryIn,
  input  [1:0] Operation,
  input  a,
  input  b,
  input  Less,
  output Result,
  output Set,
  output CarryOut
);

  wire and_1_out, multiplexer_1_out, multiplexer_2_out, not_1_out, not_2_out, or_1_out;

  not not_1 (not_1_out, a);
  Multiplexer #(.enable("false")) multiplexer_1 (.in0(a), .in1(not_1_out), .out(multiplexer_1_out), .sel(Ainvert));
  not not_2 (not_2_out, b);
  Multiplexer #(.enable("false")) multiplexer_2 (.in0(b), .in1(not_2_out), .out(multiplexer_2_out), .sel(Binvert));
  and and_1 (and_1_out, multiplexer_1_out, multiplexer_2_out);
  or or_1 (or_1_out, multiplexer_1_out, multiplexer_2_out);
  Adder #(.width(1)) adder_1 (.a(multiplexer_1_out), .b(multiplexer_2_out), .out(Set), .cin(CarryIn), .cout(CarryOut));
  Multiplexer #(.select(2), .enable("false")) multiplexer_3 (
    .in0(and_1_out), .in1(or_1_out), .in2(Set), .in3(Less), .out(Result), .sel(Operation));
endmodule

module sixteen_bit_ALU (
  input  [3:0] ALUOperation,
  input  [15:0] a,
  input  [15:0] b,
  output Zero,
  output [15:0] Result,
  output Overflow
);

  wire one_bit_alu_1_carryout, one_bit_alu_2_carryout, one_bit_alu_3_carryout, one_bit_alu_4_carryout,
       one_bit_alu_5_carryout, one_bit_alu_6_carryout, one_bit_alu_7_carryout, one_bit_alu_8_carryout,
       one_bit_alu_9_carryout, one_bit_alu_10_carryout, one_bit_alu_11_carryout, one_bit_alu_12_carryout,
       one_bit_alu_13_carryout, one_bit_alu_14_carryout, one_bit_alu_15_carryout, one_bit_alu_16_carryout,
       one_bit_alu_16_set, xor_1_out;

  one_bit_ALU one_bit_alu_1 (
    .a(a[0]), .b(b[0]), .Less(xor_1_out), .Ainvert(ALUOperation[3]), .Binvert(ALUOperation[2]),
    .CarryIn(ALUOperation[2]), .Operation(ALUOperation[1:0]), .CarryOut(one_bit_alu_1_carryout),
    .Result(Result[0]));  // open: Set
  one_bit_ALU one_bit_alu_2 (
    .a(a[1]), .b(b[1]), .Less(1'b0), .Ainvert(ALUOperation[3]), .Binvert(ALUOperation[2]),
    .CarryIn(one_bit_alu_1_carryout), .Operation(ALUOperation[1:0]), .CarryOut(one_bit_alu_2_carryout),
    .Result(Result[1]));  // open: Set
  one_bit_ALU one_bit_alu_3 (
    .a(a[2]), .b(b[2]), .Less(1'b0), .Ainvert(ALUOperation[3]), .Binvert(ALUOperation[2]),
    .CarryIn(one_bit_alu_2_carryout), .Operation(ALUOperation[1:0]), .CarryOut(one_bit_alu_3_carryout),
    .Result(Result[2]));  // open: Set
  one_bit_ALU one_bit_alu_4 (
    .a(a[3]), .b(b[3]), .Less(1'b0), .Ainvert(ALUOperation[3]), .Binvert(ALUOperation[2]),
    .CarryIn(one_bit_alu_3_carryout), .Operation(ALUOperation[1:0]), .CarryOut(one_bit_alu_4_carryout),
    .Result(Result[3]));  // open: Set
  one_bit_ALU one_bit_alu_5 (
    .a(a[4]), .b(b[4]), .Less(1'b0), .Ainvert(ALUOperation[3]), .Binvert(ALUOperation[2]),
    .CarryIn(one_bit_alu_4_carryout), .Operation(ALUOperation[1:0]), .CarryOut(one_bit_alu_5_carryout),
    .Result(Result[4]));  // open: Set
  one_bit_ALU one_bit_alu_6 (
    .a(a[5]), .b(b[5]), .Less(1'b0), .Ainvert(ALUOperation[3]), .Binvert(ALUOperation[2]),
    .CarryIn(one_bit_alu_5_carryout), .Operation(ALUOperation[1:0]), .CarryOut(one_bit_alu_6_carryout),
    .Result(Result[5]));  // open: Set
  one_bit_ALU one_bit_alu_7 (
    .a(a[6]), .b(b[6]), .Less(1'b0), .Ainvert(ALUOperation[3]), .Binvert(ALUOperation[2]),
    .CarryIn(one_bit_alu_6_carryout), .Operation(ALUOperation[1:0]), .CarryOut(one_bit_alu_7_carryout),
    .Result(Result[6]));  // open: Set
  one_bit_ALU one_bit_alu_8 (
    .a(a[7]), .b(b[7]), .Less(1'b0), .Ainvert(ALUOperation[3]), .Binvert(ALUOperation[2]),
    .CarryIn(one_bit_alu_7_carryout), .Operation(ALUOperation[1:0]), .CarryOut(one_bit_alu_8_carryout),
    .Result(Result[7]));  // open: Set
  one_bit_ALU one_bit_alu_9 (
    .a(a[8]), .b(b[8]), .Less(1'b0), .Ainvert(ALUOperation[3]), .Binvert(ALUOperation[2]),
    .CarryIn(one_bit_alu_8_carryout), .Operation(ALUOperation[1:0]), .CarryOut(one_bit_alu_9_carryout),
    .Result(Result[8]));  // open: Set
  one_bit_ALU one_bit_alu_10 (
    .a(a[9]), .b(b[9]), .Less(1'b0), .Ainvert(ALUOperation[3]), .Binvert(ALUOperation[2]),
    .CarryIn(one_bit_alu_9_carryout), .Operation(ALUOperation[1:0]), .CarryOut(one_bit_alu_10_carryout),
    .Result(Result[9]));  // open: Set
  one_bit_ALU one_bit_alu_11 (
    .a(a[10]), .b(b[10]), .Less(1'b0), .Ainvert(ALUOperation[3]), .Binvert(ALUOperation[2]),
    .CarryIn(one_bit_alu_10_carryout), .Operation(ALUOperation[1:0]), .CarryOut(one_bit_alu_11_carryout),
    .Result(Result[10]));  // open: Set
  one_bit_ALU one_bit_alu_12 (
    .a(a[11]), .b(b[11]), .Less(1'b0), .Ainvert(ALUOperation[3]), .Binvert(ALUOperation[2]),
    .CarryIn(one_bit_alu_11_carryout), .Operation(ALUOperation[1:0]), .CarryOut(one_bit_alu_12_carryout),
    .Result(Result[11]));  // open: Set
  one_bit_ALU one_bit_alu_13 (
    .a(a[12]), .b(b[12]), .Less(1'b0), .Ainvert(ALUOperation[3]), .Binvert(ALUOperation[2]),
    .CarryIn(one_bit_alu_12_carryout), .Operation(ALUOperation[1:0]), .CarryOut(one_bit_alu_13_carryout),
    .Result(Result[12]));  // open: Set
  one_bit_ALU one_bit_alu_14 (
    .a(a[13]), .b(b[13]), .Less(1'b0), .Ainvert(ALUOperation[3]), .Binvert(ALUOperation[2]),
    .CarryIn(one_bit_alu_13_carryout), .Operation(ALUOperation[1:0]), .CarryOut(one_bit_alu_14_carryout),
    .Result(Result[13]));  // open: Set
  one_bit_ALU one_bit_alu_15 (
    .a(a[14]), .b(b[14]), .Less(1'b0), .Ainvert(ALUOperation[3]), .Binvert(ALUOperation[2]),
    .CarryIn(one_bit_alu_14_carryout), .Operation(ALUOperation[1:0]), .CarryOut(one_bit_alu_15_carryout),
    .Result(Result[14]));  // open: Set
  one_bit_ALU one_bit_alu_16 (
    .a(a[15]), .b(b[15]), .Less(1'b0), .Ainvert(ALUOperation[3]), .Binvert(ALUOperation[2]),
    .CarryIn(one_bit_alu_15_carryout), .Operation(ALUOperation[1:0]), .CarryOut(one_bit_alu_16_carryout),
    .Result(Result[15]), .Set(one_bit_alu_16_set));
  xor xor_1 (xor_1_out, one_bit_alu_16_set, Overflow);
  xor xor_2 (Overflow, one_bit_alu_15_carryout, one_bit_alu_16_carryout);
  nor nor_1 (Zero, Result[0], Result[1], Result[2], Result[3], Result[4], Result[5], Result[6], Result[7], Result[8], Result[9], Result[10], Result[11], Result[12], Result[13], Result[14], Result[15]);
endmodule

module PCDecoder (
  input  [3:0] Opcode,
  input  Subop,
  input  Zero,
  input  Less,
  output RegtoPC,
  output IMMtoPC,
  output ZerosToALU,
  output [3:0] ALUOp
);

  wire and_4_out, and_5_out, and_6_out, and_7_out, and_8_out, not_1_out, not_2_out, not_3_out, not_4_out,
       not_5_out, not_6_out, not_7_out, not_8_out, not_9_out, not_10_out, not_11_out, not_12_out, not_13_out,
       not_14_out, not_15_out, not_16_out;

  not not_1 (not_1_out, Opcode[2]);
  not not_2 (not_2_out, Opcode[1]);
  not not_3 (not_3_out, Subop);
  not not_4 (not_4_out, Opcode[2]);
  not not_5 (not_5_out, Opcode[1]);
  not not_6 (not_6_out, Opcode[0]);
  not not_7 (not_7_out, Opcode[2]);
  not not_8 (not_8_out, Opcode[1]);
  not not_9 (not_9_out, Zero);
  not not_10 (not_10_out, Opcode[2]);
  not not_11 (not_11_out, Zero);
  not not_12 (not_12_out, Opcode[0]);
  not not_13 (not_13_out, Zero);
  not not_14 (not_14_out, Less);
  not not_15 (not_15_out, Opcode[0]);
  and and_1 (ZerosToALU, Opcode[3], not_16_out);
  not not_16 (not_16_out, Opcode[2]);
  and and_2 (ALUOp[1], Opcode[3], not_1_out);
  and and_3 (RegtoPC, Opcode[3], Opcode[2], not_2_out, Opcode[0], not_3_out);
  and and_4 (and_4_out, Opcode[3], not_4_out, not_5_out, not_6_out, Zero);
  and and_5 (and_5_out, Opcode[3], not_7_out, not_8_out, Opcode[0], not_9_out);
  and and_6 (and_6_out, Opcode[3], not_10_out, Opcode[0], not_11_out, Less);
  and and_7 (and_7_out, Opcode[3], Opcode[1], not_12_out, not_13_out, not_14_out);
  and and_8 (and_8_out, Opcode[3], Opcode[2], Opcode[1], not_15_out);
  or or_1 (IMMtoPC, and_4_out, and_5_out, and_6_out, and_7_out, and_8_out);

  assign {ALUOp[3:2], ALUOp[0]} = 3'b000;
endmodule

module PCDecoderLogic (
  input  Opcode3,
  input  Opcode2,
  input  Opcode1,
  input  Opcode0,
  input  Subop,
  input  Zero,
  input  Less,
  output RegtoPC,
  output IMMtoPC,
  output OnestoALU
);

  wire and_2_out, and_3_out, and_4_out, and_5_out, and_6_out, not_1_out, not_2_out, not_3_out, not_4_out,
       not_5_out, not_6_out, not_7_out, not_8_out, not_9_out, not_10_out, not_11_out, not_12_out, not_13_out,
       not_14_out, not_15_out;

  not not_1 (not_1_out, Opcode1);
  not not_2 (not_2_out, Subop);
  not not_3 (not_3_out, Opcode2);
  not not_4 (not_4_out, Opcode1);
  not not_5 (not_5_out, Opcode0);
  not not_6 (not_6_out, Opcode2);
  not not_7 (not_7_out, Opcode1);
  not not_8 (not_8_out, Zero);
  not not_9 (not_9_out, Opcode2);
  not not_10 (not_10_out, Zero);
  not not_11 (not_11_out, Opcode0);
  not not_12 (not_12_out, Zero);
  not not_13 (not_13_out, Less);
  not not_14 (not_14_out, Opcode0);
  not not_15 (not_15_out, Opcode2);
  and and_1 (RegtoPC, Opcode3, Opcode2, not_1_out, Opcode0, not_2_out);
  and and_2 (and_2_out, Opcode3, not_3_out, not_4_out, not_5_out, Zero);
  and and_3 (and_3_out, Opcode3, not_6_out, not_7_out, Opcode0, not_8_out);
  and and_4 (and_4_out, Opcode3, not_9_out, Opcode0, not_10_out, Less);
  and and_5 (and_5_out, Opcode3, Opcode1, not_11_out, not_12_out, not_13_out);
  and and_6 (and_6_out, Opcode3, Opcode2, Opcode1, not_14_out);
  and and_7 (OnestoALU, Opcode3, not_15_out);
  or or_1 (IMMtoPC, and_2_out, and_3_out, and_4_out, and_5_out, and_6_out);
endmodule

module Decoder (
  input  [3:0] Opcode,
  input  Subop,
  input  Zero,
  input  Less,
  input  Clock,
  output ShiftSrc,
  output ShifterToReg,
  output RegWrite,
  output [3:0] ALUOp,
  output IMMtoALU,
  output RegtoPC,
  output IMMtoPC,
  output ZerosToALU,
  output MemWrite,
  output MemtoReg,
  output Halt,
  output LED,
  output WriteLED,
  output MemRead,
  output PCtoReg
);

  wire Arith_LogDecoder_regwrite, d_ff_1_q, JALDecoder_regwrite, MemDecoder_regwrite, PCDecoder_immtopc,
       ShifterDecoder_regwrite;
  wire [3:0] Arith_LogDecoder_aluoperation, PCDecoder_2_aluop, register_1_q;

  D_Flip_Flop d_ff_1 (.clk(Clock), .D(Subop), .Q(d_ff_1_q), .en(1'b1));  // open: Qn, preset, reset
  Register #(.width(4)) register_1 (.D(Opcode), .en(1'b1), .Q(register_1_q), .clk(Clock));  // open: clr
  PCDecoder PCDecoder (
    .Opcode(register_1_q), .Subop(d_ff_1_q), .Zero(Zero), .Less(Less), .RegtoPC(RegtoPC),
    .IMMtoPC(PCDecoder_immtopc));  // open: ZerosToALU, ALUOp
  ShifterDecoder ShifterDecoder (
    .Opcode(Opcode), .ShiftSrc(ShiftSrc), .ShiftertoReg(ShifterToReg), .RegWrite(ShifterDecoder_regwrite));
  Arith_Log_Decoder Arith_LogDecoder (
    .Opcode(Opcode), .Subop(Subop), .ALUOperation(Arith_LogDecoder_aluoperation),
    .RegWrite(Arith_LogDecoder_regwrite), .ALUSrc(IMMtoALU));
  PCDecoder PCDecoder_2 (
    .Opcode(Opcode), .Subop(Subop), .Zero(Zero), .Less(Less), .ZerosToALU(ZerosToALU),
    .ALUOp(PCDecoder_2_aluop));  // open: RegtoPC, IMMtoPC
  MemDecoder MemDecoder (
    .Opcode(Opcode), .Subop(Subop), .MemWrite(MemWrite), .MemtoReg(MemtoReg), .RegWrite(MemDecoder_regwrite),
    .MemRead(MemRead));
  HaltDecoder haltdecoder_1 (.Opcode(Opcode), .Halt(Halt), .LED(LED));
  PutDecoder PutDecoder (.Opcode(Opcode), .WriteLED(WriteLED));
  JALDecoder JALDecoder (.Opcode(register_1_q), .IMMtoPC(PCtoReg), .PCtoReg(PCtoReg), .RegWrite(JALDecoder_regwrite));
  or or_1 (RegWrite, ShifterDecoder_regwrite, Arith_LogDecoder_regwrite, MemDecoder_regwrite, JALDecoder_regwrite);
  or or_2 (IMMtoPC, PCDecoder_immtopc, PCtoReg);
  assign ALUOp = Arith_LogDecoder_aluoperation | PCDecoder_2_aluop;  // OR_Gate or_3, 4 bits wide
endmodule

module MemDecoder (
  input  [3:0] Opcode,
  input  Subop,
  output MemWrite,
  output MemtoReg,
  output RegWrite,
  output MemRead
);

  and and_1 (MemWrite, ~Opcode[0], Opcode[1], Opcode[2], ~Opcode[3], Subop);  // AND_Gate
  and and_2 (MemRead, ~Opcode[0], Opcode[1], Opcode[2], ~Opcode[3], ~Subop);  // AND_Gate

  assign MemtoReg = MemRead;
  assign RegWrite = MemRead;
endmodule

module HaltDecoder (
  input  [3:0] Opcode,
  output Halt,
  output LED
);

  and and_1 (Halt, ~Opcode[3], Opcode[2], Opcode[1], Opcode[0]);  // AND_Gate

  assign LED = Halt;
endmodule

module PutDecoder (
  input  [3:0] Opcode,
  output WriteLED
);

  and and_1 (WriteLED, Opcode[0], Opcode[1], Opcode[2], Opcode[3]);
endmodule

module JALDecoder (
  input  [3:0] Opcode,
  output IMMtoPC,
  output PCtoReg,
  output RegWrite
);

  and and_1 (IMMtoPC, ~Opcode[0], ~Opcode[1], Opcode[2], Opcode[3]);  // AND_Gate

  assign PCtoReg = IMMtoPC;
  assign RegWrite = IMMtoPC;
endmodule

module ResultToLess (
  input  [15:0] Result,
  output Less
);


  assign Less = Result[15];
endmodule

module side (
  input  Op3,
  input  Op2,
  input  Op1,
  input  Op0,
  output Op3_2,
  output Op2_2,
  output Op1_2,
  output Op0_2
);

  wire not_1_out;

  and and_1 (Op1_2, Op3, not_1_out);
  not not_1 (not_1_out, Op2);

  assign Op0_2 = 1'b0;
  assign Op2_2 = 1'b0;
  assign Op3_2 = 1'b0;
endmodule

module ID_EX (
  input  clear,
  input  [15:0] Read_Data_1,
  input  [15:0] Read_Data_2,
  input  [15:0] IMM,
  input  SubOP,
  input  [3:0] ShiftAmount,
  input  [7:0] PC_4,
  input  ShiftSrc,
  input  ShifterToReg,
  input  RegWrite,
  input  [3:0] ALUOp,
  input  IMMtoALU,
  input  [2:0] WriteReg,
  input  ZerosToALU,
  input  MemWrite,
  input  MemToReg,
  input  SubOp_2,
  input  LED,
  input  WriteLED,
  input  MemRead,
  input  PCtoReg,
  input  Clock,
  output [15:0] Read_Data_1_2,
  output [15:0] Read_Data_2_2,
  output [15:0] IMM_2,
  output SubOP_3,
  output [3:0] ShiftAmount_2,
  output [7:0] PC_4_2,
  output ShiftSrc_2,
  output ShifterToReg_2,
  output RegWrite_2,
  output [3:0] ALUOp_2,
  output IMMtoALU_2,
  output [2:0] out_34,
  output ZerostoALU_2,
  output MemWrite_2,
  output MemToReg_2,
  output SubOp_4,
  output LED_2,
  output WriteLED_2,
  output MemRead_2,
  output PCtoReg_2
);

  Register #(.width(16)) register_1 (.D(Read_Data_1), .en(1'b1), .Q(Read_Data_1_2), .clk(Clock), .clr(clear));
  Register #(.width(16)) register_2 (.D(Read_Data_2), .en(1'b1), .Q(Read_Data_2_2), .clk(Clock), .clr(clear));
  Register #(.width(16)) register_3 (.D(IMM), .en(1'b1), .Q(IMM_2), .clk(Clock), .clr(clear));
  Register #(.width(1)) register_4 (.D(SubOP), .en(1'b1), .Q(SubOP_3), .clk(Clock), .clr(clear));
  Register #(.width(4)) register_5 (.D(ShiftAmount), .en(1'b1), .Q(ShiftAmount_2), .clk(Clock), .clr(clear));
  Register register_6 (.D(PC_4), .en(1'b1), .Q(PC_4_2), .clk(Clock), .clr(clear));
  Register #(.width(1)) register_7 (.D(ShiftSrc), .en(1'b1), .Q(ShiftSrc_2), .clk(Clock), .clr(clear));
  Register #(.width(1)) register_8 (.D(ShifterToReg), .en(1'b1), .Q(ShifterToReg_2), .clk(Clock), .clr(clear));
  Register #(.width(1)) register_9 (.D(RegWrite), .en(1'b1), .Q(RegWrite_2), .clk(Clock), .clr(clear));
  Register #(.width(4)) register_10 (.D(ALUOp), .en(1'b1), .Q(ALUOp_2), .clk(Clock), .clr(clear));
  Register #(.width(1)) register_11 (.D(IMMtoALU), .en(1'b1), .Q(IMMtoALU_2), .clk(Clock), .clr(clear));
  Register #(.width(3)) register_12 (.D(WriteReg), .en(1'b1), .Q(out_34), .clk(Clock), .clr(clear));
  Register #(.width(1)) register_13 (.D(ZerosToALU), .en(1'b1), .Q(ZerostoALU_2), .clk(Clock), .clr(clear));
  Register #(.width(1)) register_14 (.D(MemWrite), .en(1'b1), .Q(MemWrite_2), .clk(Clock), .clr(clear));
  Register #(.width(1)) register_15 (.D(MemToReg), .en(1'b1), .Q(MemToReg_2), .clk(Clock), .clr(clear));
  Register #(.width(1)) register_16 (.D(SubOp_2), .en(1'b1), .Q(SubOp_4), .clk(Clock), .clr(clear));
  Register #(.width(1)) register_17 (.D(LED), .en(1'b1), .Q(LED_2), .clk(Clock), .clr(clear));
  Register #(.width(1)) register_18 (.D(WriteLED), .en(1'b1), .Q(WriteLED_2), .clk(Clock), .clr(clear));
  Register #(.width(1)) register_19 (.D(MemRead), .en(1'b1), .Q(MemRead_2), .clk(Clock), .clr(clear));
  Register #(.width(1)) register_20 (.D(PCtoReg), .en(1'b1), .Q(PCtoReg_2), .clk(Clock), .clr(clear));
endmodule

module IF_ID (
  input  Flush,
  input  [7:0] PC_4,
  input  [15:0] Instruction,
  input  Enable,
  input  CLK,
  output [7:0] PC_4_2,
  output [15:0] Instructions
);

  wire not_1_out;
  wire [15:0] multiplexer_1_out;

  not not_1 (not_1_out, Enable);
  Multiplexer #(.width(16), .enable("false")) multiplexer_1 (
    .in0(Instruction), .in1(16'h1000), .out(multiplexer_1_out), .sel(Flush));
  Register register_1 (.D(PC_4), .en(not_1_out), .Q(PC_4_2), .clk(CLK));  // open: clr
  Register #(.width(16)) register_2 (.D(multiplexer_1_out), .en(not_1_out), .Q(Instructions), .clk(CLK));  // open: clr
endmodule

module EX_MEM (
  input  [15:0] Result,
  input  [7:0] Address,
  input  SubOP,
  input  [15:0] Read_Data_1,
  input  [15:0] ShiftOut,
  input  ShiftSrc,
  input  [3:0] ShiftAmount,
  input  [15:0] PC_4EXT,
  input  ShifterToReg,
  input  RegWrite,
  input  [2:0] WriteReg,
  input  MemWrite,
  input  MemToReg,
  input  Halt,
  input  LED,
  input  WriteLED,
  input  MemRead,
  input  PCtoReg,
  input  Clock,
  output [15:0] Result_2,
  output [7:0] Address_2,
  output SubOP_2,
  output [15:0] Read_Data_1_2,
  output [15:0] ShiftOut_2,
  output ShiftSrc_2,
  output [3:0] ShiftAmount_2,
  output [15:0] PC_4EXT_2,
  output ShifterToReg_2,
  output RegWrite_2,
  output [2:0] WriteReg_2,
  output MemWrite_2,
  output MemToReg_2,
  output Halt_2,
  output LED_2,
  output WriteLED_2,
  output MemRead_2,
  output PCtoReg_2
);

  Register #(.width(16)) register_1 (.D(Result), .en(1'b1), .Q(Result_2), .clk(Clock));  // open: clr
  Register register_2 (.D(Address), .en(1'b1), .Q(Address_2), .clk(Clock));  // open: clr
  Register #(.width(1)) register_3 (.D(SubOP), .en(1'b1), .Q(SubOP_2), .clk(Clock));  // open: clr
  Register #(.width(16)) register_4 (.D(Read_Data_1), .en(1'b1), .Q(Read_Data_1_2), .clk(Clock));  // open: clr
  Register #(.width(16)) register_5 (.D(ShiftOut), .en(1'b1), .Q(ShiftOut_2), .clk(Clock));  // open: clr
  Register #(.width(1)) register_6 (.D(ShiftSrc), .en(1'b1), .Q(ShiftSrc_2), .clk(Clock));  // open: clr
  Register #(.width(4)) register_7 (.D(ShiftAmount), .en(1'b1), .Q(ShiftAmount_2), .clk(Clock));  // open: clr
  Register #(.width(16)) register_8 (.D(PC_4EXT), .en(1'b1), .Q(PC_4EXT_2), .clk(Clock));  // open: clr
  Register #(.width(1)) register_9 (.D(ShifterToReg), .en(1'b1), .Q(ShifterToReg_2), .clk(Clock));  // open: clr
  Register #(.width(1)) register_10 (.D(RegWrite), .en(1'b1), .Q(RegWrite_2), .clk(Clock));  // open: clr
  Register #(.width(3)) register_11 (.D(WriteReg), .en(1'b1), .Q(WriteReg_2), .clk(Clock));  // open: clr
  Register #(.width(1)) register_12 (.D(MemWrite), .en(1'b1), .Q(MemWrite_2), .clk(Clock));  // open: clr
  Register #(.width(1)) register_13 (.D(MemToReg), .en(1'b1), .Q(MemToReg_2), .clk(Clock));  // open: clr
  Register #(.width(1)) register_14 (.D(Halt), .en(1'b1), .Q(Halt_2), .clk(Clock));  // open: clr
  Register #(.width(1)) register_15 (.D(LED), .en(1'b1), .Q(LED_2), .clk(Clock));  // open: clr
  Register #(.width(1)) register_16 (.D(WriteLED), .en(1'b1), .Q(WriteLED_2), .clk(Clock));  // open: clr
  Register #(.width(1)) register_17 (.D(MemRead), .en(1'b1), .Q(MemRead_2), .clk(Clock));  // open: clr
  Register #(.width(1)) register_18 (.D(PCtoReg), .en(1'b1), .Q(PCtoReg_2), .clk(Clock));  // open: clr
endmodule

module MEM_WB (
  input  [15:0] D,
  input  [15:0] Result,
  input  ShifterToReg,
  input  SubOP,
  input  [15:0] ReadData1,
  input  [15:0] ShiftOut,
  input  Shiftsrc,
  input  [3:0] ShiftAmount,
  input  [15:0] PC_4EXT,
  input  RegWrite,
  input  [2:0] WriteReg,
  input  MemToReg,
  input  Halt,
  input  LED,
  input  WriteLED,
  input  PCtoReg,
  input  in_17,
  output [15:0] D_2,
  output [15:0] Result_2,
  output ShifterToReg_2,
  output SubOP_2,
  output [15:0] ReadData1_2,
  output [15:0] ShiftOut_2,
  output ShiftSrc_2,
  output [3:0] ShiftAmount_2,
  output [15:0] PC_4EXT_2,
  output RegWrite_2,
  output [2:0] WriteReg_2,
  output MemToReg_2,
  output Halt_2,
  output LED_2,
  output WriteLED_2,
  output PCtoReg_2
);

  Register #(.width(16)) register_1 (.D(D), .en(1'b1), .Q(D_2), .clk(in_17));  // open: clr
  Register #(.width(16)) register_2 (.D(Result), .en(1'b1), .Q(Result_2), .clk(in_17));  // open: clr
  Register #(.width(1)) register_3 (.D(ShifterToReg), .en(1'b1), .Q(ShifterToReg_2), .clk(in_17));  // open: clr
  Register #(.width(1)) register_4 (.D(SubOP), .en(1'b1), .Q(SubOP_2), .clk(in_17));  // open: clr
  Register #(.width(16)) register_5 (.D(ReadData1), .en(1'b1), .Q(ReadData1_2), .clk(in_17));  // open: clr
  Register #(.width(16)) register_6 (.D(ShiftOut), .en(1'b1), .Q(ShiftOut_2), .clk(in_17));  // open: clr
  Register #(.width(1)) register_7 (.D(Shiftsrc), .en(1'b1), .Q(ShiftSrc_2), .clk(in_17));  // open: clr
  Register #(.width(4)) register_8 (.D(ShiftAmount), .en(1'b1), .Q(ShiftAmount_2), .clk(in_17));  // open: clr
  Register #(.width(16)) register_9 (.D(PC_4EXT), .en(1'b1), .Q(PC_4EXT_2), .clk(in_17));  // open: clr
  Register #(.width(1)) register_10 (.D(RegWrite), .en(1'b1), .Q(RegWrite_2), .clk(in_17));  // open: clr
  Register #(.width(3)) register_11 (.D(WriteReg), .en(1'b1), .Q(WriteReg_2), .clk(in_17));  // open: clr
  Register #(.width(1)) register_12 (.D(MemToReg), .en(1'b1), .Q(MemToReg_2), .clk(in_17));  // open: clr
  Register #(.width(1)) register_13 (.D(Halt), .en(1'b1), .Q(Halt_2), .clk(in_17));  // open: clr
  Register #(.width(1)) register_14 (.D(LED), .en(1'b1), .Q(LED_2), .clk(in_17));  // open: clr
  Register #(.width(1)) register_15 (.D(WriteLED), .en(1'b1), .Q(WriteLED_2), .clk(in_17));  // open: clr
  Register #(.width(1)) register_16 (.D(PCtoReg), .en(1'b1), .Q(PCtoReg_2), .clk(in_17));  // open: clr
endmodule

module FlushDetector (
  input  IMMtoPC,
  input  RegToPC,
  input  [7:0] NormalPC,
  input  [7:0] JPC,
  output flush,
  output [7:0] NewPC
);

  or or_1 (flush, IMMtoPC, RegToPC);
  Multiplexer #(.width(8), .enable("false")) multiplexer_1 (.in0(NormalPC), .in1(JPC), .out(NewPC), .sel(flush));
endmodule

// Forwarding
module ForwardUnit (
  input  [2:0] WriteReg,
  input  RegWrite,
  input  [2:0] ReadReg1,
  input  [2:0] ReadReg2,
  input  ImmToALU,
  input  Clock,
  output _1FromWB,
  output _2FromWB,
  output Hazard,
  output _1FromALU,
  output _2FromALU,
  output _1FromMem,
  output _2FromMem,
  output Reg1Toggle,
  output Reg2Toggle
);

  wire d_ff_1_q, d_ff_2_q, d_ff_3_q, d_ff_4_q, d_ff_5_q, d_ff_6_q, d_ff_7_q, d_ff_8_q, d_ff_9_q, d_ff_10_q,
       d_ff_11_q, d_ff_12_q, nor_1_out, nor_2_out, nor_3_out, nor_4_out, nor_5_out, nor_6_out, not_1_out,
       xor_1_out, xor_2_out, xor_3_out, xor_4_out, xor_5_out, xor_6_out, xor_7_out, xor_8_out, xor_9_out,
       xor_10_out, xor_11_out, xor_12_out, xor_13_out, xor_14_out, xor_15_out, xor_16_out, xor_17_out,
       xor_18_out;

  not not_1 (not_1_out, ImmToALU);
  D_Flip_Flop d_ff_1 (.clk(Clock), .D(WriteReg[0]), .Q(d_ff_1_q), .en(1'b1));  // open: Qn, preset, reset
  D_Flip_Flop d_ff_2 (.clk(Clock), .D(WriteReg[1]), .Q(d_ff_2_q));  // open: Qn, preset, en, reset
  D_Flip_Flop d_ff_3 (.clk(Clock), .D(WriteReg[2]), .Q(d_ff_3_q), .en(1'b1));  // open: Qn, preset, reset
  D_Flip_Flop d_ff_4 (.clk(Clock), .D(RegWrite), .Q(d_ff_4_q), .en(1'b1));  // open: Qn, preset, reset
  xor xor_1 (xor_1_out, d_ff_1_q, ReadReg1[0]);
  xor xor_2 (xor_2_out, d_ff_2_q, ReadReg1[1]);
  xor xor_3 (xor_3_out, d_ff_3_q, ReadReg1[2]);
  xor xor_4 (xor_4_out, d_ff_1_q, ReadReg2[0]);
  xor xor_5 (xor_5_out, d_ff_2_q, ReadReg2[1]);
  xor xor_6 (xor_6_out, d_ff_3_q, ReadReg2[2]);
  D_Flip_Flop d_ff_5 (.clk(Clock), .D(d_ff_1_q), .Q(d_ff_5_q), .en(1'b1));  // open: Qn, preset, reset
  D_Flip_Flop d_ff_6 (.clk(Clock), .D(d_ff_2_q), .Q(d_ff_6_q), .en(1'b1));  // open: Qn, preset, reset
  D_Flip_Flop d_ff_7 (.clk(Clock), .D(d_ff_3_q), .Q(d_ff_7_q), .en(1'b1));  // open: Qn, preset, reset
  D_Flip_Flop d_ff_8 (.clk(Clock), .D(d_ff_4_q), .Q(d_ff_8_q), .en(1'b1));  // open: Qn, preset, reset
  and and_1 (_1FromALU, d_ff_4_q, nor_1_out);
  nor nor_1 (nor_1_out, xor_1_out, xor_2_out, xor_3_out);
  and and_2 (_2FromALU, d_ff_4_q, not_1_out, nor_2_out);
  nor nor_2 (nor_2_out, xor_4_out, xor_5_out, xor_6_out);
  xor xor_7 (xor_7_out, d_ff_5_q, ReadReg1[0]);
  xor xor_8 (xor_8_out, d_ff_6_q, ReadReg1[1]);
  xor xor_9 (xor_9_out, d_ff_7_q, ReadReg1[2]);
  xor xor_10 (xor_10_out, d_ff_5_q, ReadReg2[0]);
  xor xor_11 (xor_11_out, d_ff_6_q, ReadReg2[1]);
  xor xor_12 (xor_12_out, d_ff_7_q, ReadReg2[2]);
  D_Flip_Flop d_ff_9 (.clk(Clock), .D(d_ff_5_q), .Q(d_ff_9_q), .en(1'b1));  // open: Qn, preset, reset
  D_Flip_Flop d_ff_10 (.clk(Clock), .D(d_ff_6_q), .Q(d_ff_10_q), .en(1'b1));  // open: Qn, preset, reset
  D_Flip_Flop d_ff_11 (.clk(Clock), .D(d_ff_7_q), .Q(d_ff_11_q), .en(1'b1));  // open: Qn, preset, reset
  D_Flip_Flop d_ff_12 (.clk(Clock), .D(d_ff_8_q), .Q(d_ff_12_q), .en(1'b1));  // open: Qn, preset, reset
  and and_3 (_1FromMem, d_ff_8_q, nor_3_out);
  nor nor_3 (nor_3_out, xor_7_out, xor_8_out, xor_9_out);
  and and_4 (_2FromMem, d_ff_8_q, not_1_out, nor_4_out);
  nor nor_4 (nor_4_out, xor_10_out, xor_11_out, xor_12_out);
  xor xor_13 (xor_13_out, d_ff_9_q, ReadReg2[0]);
  xor xor_14 (xor_14_out, d_ff_10_q, ReadReg2[1]);
  xor xor_15 (xor_15_out, d_ff_11_q, ReadReg2[2]);
  xor xor_16 (xor_16_out, d_ff_9_q, ReadReg1[0]);
  nor nor_5 (nor_5_out, xor_16_out, xor_17_out, xor_18_out);
  xor xor_17 (xor_17_out, d_ff_11_q, ReadReg1[1]);
  xor xor_18 (xor_18_out, d_ff_10_q, ReadReg1[2]);
  nor nor_6 (nor_6_out, xor_13_out, xor_14_out, xor_15_out);
  and and_5 (_1FromWB, d_ff_12_q, nor_5_out);
  and and_6 (_2FromWB, d_ff_12_q, nor_6_out, not_1_out);
  or or_1 (Hazard, _1FromWB, _1FromMem, _1FromALU, _2FromWB, _2FromMem, _2FromALU);
  or or_2 (Reg1Toggle, _1FromWB, _1FromMem, _1FromALU);
  or or_3 (Reg2Toggle, _2FromWB, _2FromMem, _2FromALU);
endmodule

module MemForward (
  input  [2:0] memReg,
  input  [2:0] nextReg1,
  input  [2:0] nextReg2,
  input  clk,
  input  MemRead,
  output ALUSelect1,
  output ALUSelect2,
  output regSelect1,
  output regSelect2
);

  wire comparator_1_eq, comparator_2_eq, comparator_3_eq, comparator_4_eq;
  wire [2:0] register_1_q, register_2_q;

  Register #(.width(3)) register_1 (.D(nextReg1), .en(1'b1), .Q(register_1_q), .clk(clk));  // open: clr
  Register #(.width(3)) register_2 (.D(nextReg2), .en(1'b1), .Q(register_2_q), .clk(clk));  // open: clr
  Comparator #(.width(3), .mode("unsigned")) comparator_1 (
    .a(memReg), .b(register_1_q), .eq(comparator_1_eq));  // open: gt, lt
  Comparator #(.width(3), .mode("unsigned")) comparator_2 (
    .a(memReg), .b(register_2_q), .eq(comparator_2_eq));  // open: gt, lt
  Comparator #(.width(3)) comparator_3 (.a(memReg), .b(nextReg1), .eq(comparator_3_eq));  // open: gt, lt
  Comparator #(.width(3)) comparator_4 (.a(memReg), .b(nextReg2), .eq(comparator_4_eq));  // open: gt, lt
  and and_1 (ALUSelect1, comparator_1_eq, MemRead);
  and and_2 (ALUSelect2, comparator_2_eq, MemRead);
  and and_3 (regSelect1, comparator_3_eq, MemRead);
  and and_4 (regSelect2, comparator_4_eq, MemRead);
endmodule

module BubbleGen (
  input  [3:0] Opcode,
  output out_2
);

  wire comparator_1_eq, comparator_2_eq;

  Comparator #(.width(4), .mode("unsigned")) comparator_1 (
    .a(Opcode), .b(4'b1010), .eq(comparator_1_eq));  // open: gt, lt
  Comparator #(.width(4)) comparator_2 (.a(Opcode), .b(4'b1000), .eq(comparator_2_eq));  // open: gt, lt
  or or_1 (out_2, comparator_1_eq, comparator_2_eq);
endmodule
