// Logisim project ant111_lab10part1.circ as structural Verilog: 2 circuits, main circuit Register File
module main (
  input  in_1,
  input  [1:0] in_2,
  input  [1:0] in_3,
  input  [1:0] in_4,
  input  [15:0] in_5,
  output [15:0] ReadData1,
  output [15:0] ReadData2
);

  wire clock_1_out;

  Clock clock_1 (.out(clock_1_out));
  Register_File register_file_1 (
    .WriteData(in_5), .Clock(clock_1_out), .WriteEnable(in_1), .ReadRegister1(in_2), .ReadRegister2(in_3),
    .WriteRegister(in_4), .ReadData1(ReadData1), .ReadData2(ReadData2));
endmodule

module Register_File (
  input  WriteEnable,
  input  [1:0] ReadRegister1,
  input  [1:0] ReadRegister2,
  input  [1:0] WriteRegister,
  input  [15:0] WriteData,
  input  Clock,
  output [15:0] ReadData1,
  output [15:0] ReadData2
);

  wire decoder_1_out0, decoder_1_out1, decoder_1_out2, decoder_1_out3;
  wire [15:0] demultiplexer_1_out0, demultiplexer_1_out1, demultiplexer_1_out2, demultiplexer_1_out3,
       Reg_0_q, Reg_1_q, Reg_2_q, Reg_3_q;

  Demultiplexer #(.select(2), .width(16), .enable("false")) demultiplexer_1 (
    .out0(demultiplexer_1_out0), .out1(demultiplexer_1_out1), .out2(demultiplexer_1_out2),
    .out3(demultiplexer_1_out3), .in(WriteData), .sel(WriteRegister));
  Decoder #(.select(2), .enable("false")) decoder_1 (
    .out0(decoder_1_out0), .out1(decoder_1_out1), .out2(decoder_1_out2), .out3(decoder_1_out3),
    .sel(WriteRegister));
  Register #(.width(16)) Reg_0 (.D(demultiplexer_1_out0), .en(decoder_1_out0), .Q(Reg_0_q), .clk(Clock));  // open: clr
  Register #(.width(16)) Reg_1 (.D(demultiplexer_1_out1), .en(decoder_1_out1), .Q(Reg_1_q), .clk(Clock));  // open: clr
  Register #(.width(16)) Reg_2 (.D(demultiplexer_1_out2), .en(decoder_1_out2), .Q(Reg_2_q), .clk(Clock));  // open: clr
  Register #(.width(16)) Reg_3 (.D(demultiplexer_1_out3), .en(decoder_1_out3), .Q(Reg_3_q), .clk(Clock));  // open: clr
  Multiplexer #(.select(2), .width(16), .enable("false")) multiplexer_1 (
    .in0(Reg_0_q), .in1(Reg_1_q), .in2(Reg_2_q), .in3(Reg_3_q), .out(ReadData1), .sel(ReadRegister1));
  Multiplexer #(.select(2), .width(16), .enable("false")) multiplexer_2 (
    .in0(Reg_0_q), .in1(Reg_1_q), .in2(Reg_2_q), .in3(Reg_3_q), .out(ReadData2), .sel(ReadRegister2));
endmodule
