// Logisim project ant111_lab10part2.circ as structural Verilog: 1 circuit, main circuit main
module main (
  input  [7:0] Write,
  output [7:0] Read
);

  wire Clock_out, controlled_buffer_1_out, d_ff_1_qn, nand_1_out, not_1_out, Reset_out;
  wire [7:0] counter_1_q, ram_1_data;

  Clock Clock (.out(Clock_out));
  Button Reset (.out(Reset_out));
  Counter counter_1 (.Q(counter_1_q), .clk(Clock_out), .clr(Reset_out));  // open: load, D, count, carry
  nand nand_1 (nand_1_out, counter_1_q[0], counter_1_q[1], counter_1_q[2], counter_1_q[3], counter_1_q[4], counter_1_q[5], counter_1_q[6], counter_1_q[7]);
  D_Flip_Flop d_ff_1 (.clk(nand_1_out), .D(1'b1), .Qn(d_ff_1_qn), .reset(Reset_out));  // open: Q, preset, en
  assign controlled_buffer_1_out = d_ff_1_qn ? Clock_out : 1'bz;  // Controlled_Buffer controlled_buffer_1
  RAM ram_1 (
    .addr(counter_1_q), .data(ram_1_data), .clk(controlled_buffer_1_out), .ld(not_1_out), .clr(Reset_out));  // open: sel
  not not_1 (not_1_out, d_ff_1_qn);
  assign ram_1_data = d_ff_1_qn ? Write : 8'bz;  // Controlled_Buffer controlled_buffer_2
  assign Read = not_1_out ? ram_1_data : 8'bz;  // Controlled_Buffer controlled_buffer_3
endmodule
