// Logisim project ant111_lab8part2.circ as structural Verilog
module TimerAlert (
  input  Reset,
  input  Clock_input,
  output Timer_Expired,
  output Alert
);

  wire and_1_out, and_2_out, and_3_out, and_4_out, and_5_out, and_6_out, and_7_out, and_8_out;
  wire [8:0] counter_1_q;

  Counter #(.width(10), .max('h3ff), .ongoal("stay")) counter_1 (
    .Q({Alert, counter_1_q}), .clk(Clock_input), .clr(Reset));  // open: load, D, count, carry
  and and_1 (and_1_out, counter_1_q[0], counter_1_q[1]);
  and and_2 (and_2_out, and_1_out, and_3_out);
  and and_3 (and_3_out, counter_1_q[2], counter_1_q[3]);
  and and_4 (and_4_out, counter_1_q[4], counter_1_q[5]);
  and and_5 (and_5_out, counter_1_q[6], counter_1_q[7]);
  and and_6 (and_6_out, and_5_out, and_7_out);
  and and_7 (and_7_out, counter_1_q[8], Alert);
  and and_8 (and_8_out, and_2_out, and_4_out);
  and and_9 (Timer_Expired, and_8_out, and_6_out);
endmodule
