// Logisim project ant111_lab9.circ as structural Verilog
module _1_bit_ALU (
  input  A_invert,
  input  B_invert,
  input  Carry_in,
  input  [1:0] Operation,
  input  a,
  input  b,
  input  Less,
  output Result,
  output Set,
  output Carry_out
);

  wire and_1_out, multiplexer_1_out, multiplexer_2_out, not_1_out, not_2_out, or_1_out;

  not not_1 (not_1_out, a);
  Multiplexer #(.enable("false")) multiplexer_1 (.in0(a), .in1(not_1_out), .out(multiplexer_1_out), .sel(A_invert));
  not not_2 (not_2_out, b);
  Multiplexer #(.enable("false")) multiplexer_2 (.in0(b), .in1(not_2_out), .out(multiplexer_2_out), .sel(B_invert));
  and and_1 (and_1_out, multiplexer_1_out, multiplexer_2_out);
  or or_1 (or_1_out, multiplexer_1_out, multiplexer_2_out);
  Adder #(.width(1)) adder_1 (
    .a(multiplexer_1_out), .b(multiplexer_2_out), .out(Set), .cin(Carry_in), .cout(Carry_out));
  Multiplexer #(.select(2), .enable("false")) multiplexer_3 (
    .in0(and_1_out), .in1(or_1_out), .in2(Set), .in3(Less), .out(Result), .sel(Operation));
endmodule

module _8_bit__ALU (
  input  A_invert,
  input  B_invert,
  input  [1:0] Operation,
  input  [7:0] A,
  input  [7:0] B
);

  wire n1_bit_alu_1_carry_out, n1_bit_alu_2_carry_out, n1_bit_alu_3_carry_out, n1_bit_alu_4_carry_out,
       n1_bit_alu_5_carry_out, n1_bit_alu_6_carry_out, n1_bit_alu_7_carry_out;

  _1_bit_ALU u_1_bit_alu_1 (
    .a(A[0]), .b(B[0]), .A_invert(A_invert), .B_invert(B_invert), .Carry_in(B_invert), .Operation(Operation),
    .Carry_out(n1_bit_alu_1_carry_out));  // open: Less, Result, Set
  _1_bit_ALU u_1_bit_alu_2 (
    .a(A[1]), .b(B[1]), .A_invert(A_invert), .B_invert(B_invert), .Carry_in(n1_bit_alu_1_carry_out),
    .Operation(Operation), .Carry_out(n1_bit_alu_2_carry_out));  // open: Less, Result, Set
  _1_bit_ALU u_1_bit_alu_3 (
    .a(A[2]), .b(B[2]), .A_invert(A_invert), .B_invert(B_invert), .Carry_in(n1_bit_alu_2_carry_out),
    .Operation(Operation), .Carry_out(n1_bit_alu_3_carry_out));  // open: Less, Result, Set
  _1_bit_ALU u_1_bit_alu_4 (
    .a(A[3]), .b(B[3]), .A_invert(A_invert), .B_invert(B_invert), .Carry_in(n1_bit_alu_3_carry_out),
    .Operation(Operation), .Carry_out(n1_bit_alu_4_carry_out));  // open: Less, Result, Set
  _1_bit_ALU u_1_bit_alu_5 (
    .a(A[4]), .b(B[4]), .A_invert(A_invert), .B_invert(B_invert), .Carry_in(n1_bit_alu_4_carry_out),
    .Operation(Operation), .Carry_out(n1_bit_alu_5_carry_out));  // open: Less, Result, Set
  _1_bit_ALU u_1_bit_alu_6 (
    .a(A[5]), .b(B[5]), .A_invert(A_invert), .B_invert(B_invert), .Carry_in(n1_bit_alu_5_carry_out),
    .Operation(Operation), .Carry_out(n1_bit_alu_6_carry_out));  // open: Less, Result, Set
  _1_bit_ALU u_1_bit_alu_7 (
    .a(A[6]), .b(B[6]), .A_invert(A_invert), .B_invert(B_invert), .Carry_in(n1_bit_alu_6_carry_out),
    .Operation(Operation), .Carry_out(n1_bit_alu_7_carry_out));  // open: Less, Result, Set
  _1_bit_ALU u_1_bit_alu_8 (
    .a(A[7]), .b(B[7]), .A_invert(A_invert), .B_invert(B_invert), .Carry_in(n1_bit_alu_7_carry_out),
    .Operation(Operation));  // open: Less, Result, Set, Carry_out
endmodule
