// Logisim project coemips.circ as structural Verilog: 18 circuits, main circuit main
module main (
);

  wire Branch_Control_negative, Branch_Control_zero, Clear_RAM_out, Clock_out, decoder_1_unsigned,
       Halt_Control_halt, Load_Store_load, not_1_out, not_2_out, PC_Control_first, PC_Control_second,
       RegOut_s, Reset_out, Shift_Control_amount, Shift_Control_right, Write_Control_write;
  wire [1:0] MUX_Control_out_2;
  wire [2:0] decoder_1_readregister1_rs, decoder_1_readregister2_rt;
  wire [3:0] ALU_Control_aluop, decoder_1_shamt, put_control_1_hex0, put_control_1_hex1, put_control_1_hex2,
       put_control_1_hex3;
  wire [4:0] decoder_1_opcode;
  wire [7:0] adder_1_out, decoder_1_immediate, multiplexer_2_out, multiplexer_3_out, PC_q,
       registerfile_1_readdata1;
  wire [15:0] bit_extender_2_out, Bit_Extender_result, multiplexer_1_out, multiplexer_4_out,
       n16_bit_alu_1_result, ram_1_data, registerfile_1_readdata2, rom_1_data, Shifter_result;
  wire [15:8] registerfile_1_readdata1_2;

  Clock Clock (.out(Clock_out));
  Register PC (.D(multiplexer_3_out), .en(Halt_Control_halt), .Q(PC_q), .clk(Clock_out), .clr(Reset_out));
  Button Reset (.out(Reset_out));
  Adder adder_1 (.a(PC_q), .b(8'h1), .out(adder_1_out));  // open: cin, cout
  ROM #(.dataWidth(16)) rom_1 (.addr(PC_q), .data(rom_1_data), .sel(1'b1));
  Halt_Control Halt_Control (.in_1(decoder_1_opcode), .Halt(Halt_Control_halt));
  not not_1 (not_1_out, Halt_Control_halt);
  LED Halt (.in(not_1_out));
  Decoder decoder_1 (
    .Instruction(rom_1_data), .ShAmt(decoder_1_shamt), .Unsigned(decoder_1_unsigned),
    .ReadRegister2_Rt(decoder_1_readregister2_rt), .ReadRegister1_Rs(decoder_1_readregister1_rs),
    .Immediate(decoder_1_immediate), .OpCode(decoder_1_opcode));
  extender Bit_Extender (.\input (decoder_1_immediate), .Result(Bit_Extender_result), .Unsigned(decoder_1_unsigned));
  Hex_Digit_Display hex_digit_display_1 (.value(put_control_1_hex3));  // open: dp
  Hex_Digit_Display hex_digit_display_2 (.value(put_control_1_hex2));  // open: dp
  Write_Control Write_Control (.in_1(decoder_1_opcode), .write(Write_Control_write));
  Hex_Digit_Display hex_digit_display_3 (.value(put_control_1_hex1));  // open: dp
  Hex_Digit_Display hex_digit_display_4 (.value(put_control_1_hex0));  // open: dp
  Put_Control put_control_1 (
    .\input ({registerfile_1_readdata1_2, registerfile_1_readdata1}), .opCode(decoder_1_opcode),
    .Hex0(put_control_1_hex0), .Hex1(put_control_1_hex1), .Hex2(put_control_1_hex2),
    .Hex3(put_control_1_hex3), .Reset(Reset_out));
  RegisterFile registerfile_1 (
    .ReadRegister1(decoder_1_readregister1_rs), .ReadRegister2(decoder_1_readregister2_rt),
    .WriteRegister(decoder_1_readregister1_rs), .ReadData2(registerfile_1_readdata2),
    .ReadData1({registerfile_1_readdata1_2, registerfile_1_readdata1}), .WriteEnable(Write_Control_write),
    .WriteData(multiplexer_4_out), .Clock(Clock_out), .Reset(Reset_out));
  RegOut RegOut (.in_1(decoder_1_opcode), .s(RegOut_s));
  shift_control Shift_Control (.in_1(decoder_1_opcode), .amount(Shift_Control_amount), .right(Shift_Control_right));
  Branch Branch_Control (
    .in_1({registerfile_1_readdata1_2, registerfile_1_readdata1}), .Zero(Branch_Control_zero),
    .Negative(Branch_Control_negative));
  Multiplexer #(.width(16), .enable("false")) multiplexer_1 (
    .in0(registerfile_1_readdata2), .in1(Bit_Extender_result), .out(multiplexer_1_out), .sel(RegOut_s));
  Shifter Shifter (
    .Input({registerfile_1_readdata1_2, registerfile_1_readdata1}), .Shift_Value(registerfile_1_readdata2),
    .ShAmt(decoder_1_shamt), .Result(Shifter_result), .amount(Shift_Control_amount),
    .right(Shift_Control_right));
  ALUcontrol ALU_Control (.in_1(decoder_1_opcode), .ALUOp(ALU_Control_aluop));
  _16_bit_ALU u_16_bit_alu_1 (
    .A({registerfile_1_readdata1_2, registerfile_1_readdata1}), .B(multiplexer_1_out),
    .OpCode(ALU_Control_aluop), .Result(n16_bit_alu_1_result));  // open: Zero, Overflow
  PC_control PC_Control (
    .zero(Branch_Control_zero), .negative(Branch_Control_negative), .first(PC_Control_first),
    .second(PC_Control_second), .in_1(decoder_1_opcode));
  not not_2 (not_2_out, Load_Store_load);
  Multiplexer #(.width(8), .enable("false")) multiplexer_2 (
    .in0(adder_1_out), .in1(decoder_1_immediate), .out(multiplexer_2_out), .sel(PC_Control_first));
  RAM #(.dataWidth(16), .bus("separate")) ram_1 (
    .addr(registerfile_1_readdata2[7:0]), .din({registerfile_1_readdata1_2, registerfile_1_readdata1}),
    .data(ram_1_data), .str(not_2_out), .clk(Clock_out), .ld(Load_Store_load), .clr(Clear_RAM_out));  // open: sel
  Button Clear_RAM (.out(Clear_RAM_out));
  Load_Store Load_Store (.in_1(decoder_1_opcode), .load(Load_Store_load));
  assign bit_extender_2_out = {{8{1'b0}}, adder_1_out};  // Bit_Extender bit_extender_2
  Multiplexer #(.width(8), .enable("false")) multiplexer_3 (
    .in0(multiplexer_2_out), .in1(registerfile_1_readdata1), .out(multiplexer_3_out), .sel(PC_Control_second));
  MUXControl MUX_Control (.in_1(decoder_1_opcode), .out_2(MUX_Control_out_2));
  Multiplexer #(.select(2), .width(16), .enable("false")) multiplexer_4 (
    .in0(ram_1_data), .in1(n16_bit_alu_1_result), .in2(Shifter_result), .in3(bit_extender_2_out),
    .out(multiplexer_4_out), .sel(MUX_Control_out_2));

  // Notes on the sheet:
  //   Andrew Tran  - ant111
  //   ROM
  //   contents of rom_1 (hex, n*v repeats v):
  //   1 241 6001 1001 241 200 12f6 b202 10ff 6000 f000 10ff a009 8009 7000
  //   RAM
endmodule

// 4-function ALU
module _16_bit_ALU (
  input  [3:0] OpCode,
  input  [15:0] A,
  input  [15:0] B,
  output [15:0] Result,
  output Zero,
  output Overflow
);

  wire multiplexer_1_out, n1_bit_alu_1_carry_out, n1_bit_alu_2_carry_out, n1_bit_alu_3_carry_out,
       n1_bit_alu_4_carry_out, n1_bit_alu_5_carry_out, n1_bit_alu_6_carry_out, n1_bit_alu_7_carry_out,
       n1_bit_alu_8_carry_out, n1_bit_alu_9_carry_out, n1_bit_alu_10_carry_out, n1_bit_alu_11_carry_out,
       n1_bit_alu_12_carry_out, n1_bit_alu_13_carry_out, n1_bit_alu_14_carry_out, n1_bit_alu_15_carry_out,
       n1_bit_alu_16_carry_out, n1_bit_alu_16_set, not_1_out;

  Multiplexer #(.enable("false")) multiplexer_1 (
    .in0(n1_bit_alu_16_set), .in1(not_1_out), .out(multiplexer_1_out), .sel(Overflow));
  not not_1 (not_1_out, n1_bit_alu_16_set);
  _1_bit_ALU u_1_bit_alu_1 (
    .a(A[0]), .b(B[0]), .Less(multiplexer_1_out), .Result(Result[0]), .A_invert(OpCode[3]),
    .B_invert(OpCode[2]), .Carry_in(OpCode[2]), .Operation(OpCode[1:0]), .Carry_out(n1_bit_alu_1_carry_out));  // open: Set
  _1_bit_ALU u_1_bit_alu_2 (
    .a(A[1]), .b(B[1]), .Less(1'b0), .Result(Result[1]), .A_invert(OpCode[3]), .B_invert(OpCode[2]),
    .Carry_in(n1_bit_alu_1_carry_out), .Operation(OpCode[1:0]), .Carry_out(n1_bit_alu_2_carry_out));  // open: Set
  _1_bit_ALU u_1_bit_alu_3 (
    .a(A[2]), .b(B[2]), .Less(1'b0), .Result(Result[2]), .A_invert(OpCode[3]), .B_invert(OpCode[2]),
    .Carry_in(n1_bit_alu_2_carry_out), .Operation(OpCode[1:0]), .Carry_out(n1_bit_alu_3_carry_out));  // open: Set
  _1_bit_ALU u_1_bit_alu_4 (
    .a(A[3]), .b(B[3]), .Less(1'b0), .Result(Result[3]), .A_invert(OpCode[3]), .B_invert(OpCode[2]),
    .Carry_in(n1_bit_alu_3_carry_out), .Operation(OpCode[1:0]), .Carry_out(n1_bit_alu_4_carry_out));  // open: Set
  _1_bit_ALU u_1_bit_alu_5 (
    .a(A[4]), .b(B[4]), .Less(1'b0), .Result(Result[4]), .A_invert(OpCode[3]), .B_invert(OpCode[2]),
    .Carry_in(n1_bit_alu_4_carry_out), .Operation(OpCode[1:0]), .Carry_out(n1_bit_alu_5_carry_out));  // open: Set
  _1_bit_ALU u_1_bit_alu_6 (
    .a(A[5]), .b(B[5]), .Less(1'b0), .Result(Result[5]), .A_invert(OpCode[3]), .B_invert(OpCode[2]),
    .Carry_in(n1_bit_alu_5_carry_out), .Operation(OpCode[1:0]), .Carry_out(n1_bit_alu_6_carry_out));  // open: Set
  _1_bit_ALU u_1_bit_alu_7 (
    .a(A[6]), .b(B[6]), .Less(1'b0), .Result(Result[6]), .A_invert(OpCode[3]), .B_invert(OpCode[2]),
    .Carry_in(n1_bit_alu_6_carry_out), .Operation(OpCode[1:0]), .Carry_out(n1_bit_alu_7_carry_out));  // open: Set
  _1_bit_ALU u_1_bit_alu_8 (
    .a(A[7]), .b(B[7]), .Less(1'b0), .Result(Result[7]), .A_invert(OpCode[3]), .B_invert(OpCode[2]),
    .Carry_in(n1_bit_alu_7_carry_out), .Operation(OpCode[1:0]), .Carry_out(n1_bit_alu_8_carry_out));  // open: Set
  _1_bit_ALU u_1_bit_alu_9 (
    .a(A[8]), .b(B[8]), .Less(1'b0), .Result(Result[8]), .A_invert(OpCode[3]), .B_invert(OpCode[2]),
    .Carry_in(n1_bit_alu_8_carry_out), .Operation(OpCode[1:0]), .Carry_out(n1_bit_alu_9_carry_out));  // open: Set
  _1_bit_ALU u_1_bit_alu_10 (
    .a(A[9]), .b(B[9]), .Less(1'b0), .Result(Result[9]), .A_invert(OpCode[3]), .B_invert(OpCode[2]),
    .Carry_in(n1_bit_alu_9_carry_out), .Operation(OpCode[1:0]), .Carry_out(n1_bit_alu_10_carry_out));  // open: Set
  _1_bit_ALU u_1_bit_alu_11 (
    .a(A[10]), .b(B[10]), .Less(1'b0), .Result(Result[10]), .A_invert(OpCode[3]), .B_invert(OpCode[2]),
    .Carry_in(n1_bit_alu_10_carry_out), .Operation(OpCode[1:0]), .Carry_out(n1_bit_alu_11_carry_out));  // open: Set
  _1_bit_ALU u_1_bit_alu_12 (
    .a(A[11]), .b(B[11]), .Less(1'b0), .Result(Result[11]), .A_invert(OpCode[3]), .B_invert(OpCode[2]),
    .Carry_in(n1_bit_alu_11_carry_out), .Operation(OpCode[1:0]), .Carry_out(n1_bit_alu_12_carry_out));  // open: Set
  _1_bit_ALU u_1_bit_alu_13 (
    .a(A[12]), .b(B[12]), .Less(1'b0), .Result(Result[12]), .A_invert(OpCode[3]), .B_invert(OpCode[2]),
    .Carry_in(n1_bit_alu_12_carry_out), .Operation(OpCode[1:0]), .Carry_out(n1_bit_alu_13_carry_out));  // open: Set
  _1_bit_ALU u_1_bit_alu_14 (
    .a(A[13]), .b(B[13]), .Less(1'b0), .Result(Result[13]), .A_invert(OpCode[3]), .B_invert(OpCode[2]),
    .Carry_in(n1_bit_alu_13_carry_out), .Operation(OpCode[1:0]), .Carry_out(n1_bit_alu_14_carry_out));  // open: Set
  _1_bit_ALU u_1_bit_alu_15 (
    .a(A[14]), .b(B[14]), .Less(1'b0), .Result(Result[14]), .A_invert(OpCode[3]), .B_invert(OpCode[2]),
    .Carry_in(n1_bit_alu_14_carry_out), .Operation(OpCode[1:0]), .Carry_out(n1_bit_alu_15_carry_out));  // open: Set
  _1_bit_ALU u_1_bit_alu_16 (
    .a(A[15]), .b(B[15]), .Less(1'b0), .Result(Result[15]), .Set(n1_bit_alu_16_set), .A_invert(OpCode[3]),
    .B_invert(OpCode[2]), .Carry_in(n1_bit_alu_15_carry_out), .Operation(OpCode[1:0]),
    .Carry_out(n1_bit_alu_16_carry_out));
  xor xor_1 (Overflow, n1_bit_alu_15_carry_out, n1_bit_alu_16_carry_out);
  nor nor_1 (Zero, Result[0], Result[1], Result[2], Result[3], Result[4], Result[5], Result[6], Result[7], Result[8], Result[9], Result[10], Result[11], Result[12], Result[13], Result[14], Result[15]);
endmodule

module _1_bit_ALU (
  input  A_invert,
  input  B_invert,
  input  Carry_in,
  input  [1:0] Operation,
  input  a,
  input  b,
  input  Less,
  output Result,
  output Set,
  output Carry_out
);

  wire and_1_out, multiplexer_1_out, multiplexer_2_out, not_1_out, not_2_out, or_1_out;

  not not_1 (not_1_out, a);
  Multiplexer #(.enable("false")) multiplexer_1 (.in0(a), .in1(not_1_out), .out(multiplexer_1_out), .sel(A_invert));
  not not_2 (not_2_out, b);
  Multiplexer #(.enable("false")) multiplexer_2 (.in0(b), .in1(not_2_out), .out(multiplexer_2_out), .sel(B_invert));
  and and_1 (and_1_out, multiplexer_1_out, multiplexer_2_out);
  or or_1 (or_1_out, multiplexer_1_out, multiplexer_2_out);
  Adder #(.width(1)) adder_1 (
    .a(multiplexer_1_out), .b(multiplexer_2_out), .out(Set), .cin(Carry_in), .cout(Carry_out));
  Multiplexer #(.select(2), .enable("false")) multiplexer_3 (
    .in0(and_1_out), .in1(or_1_out), .in2(Set), .in3(Less), .out(Result), .sel(Operation));
endmodule

module Decoder (
  input  [15:0] Instruction,
  output [7:0] Immediate,
  output [3:0] ShAmt,
  output Unsigned,
  output [2:0] ReadRegister2_Rt,
  output [2:0] ReadRegister1_Rs,
  output [4:0] OpCode
);


  assign Immediate = Instruction[7:0];
  assign OpCode = {Instruction[15:12], Instruction[0]};
  assign ReadRegister1_Rs = Instruction[11:9];
  assign ReadRegister2_Rt = Instruction[8:6];
  assign ShAmt = Instruction[4:1];
  assign Unsigned = Instruction[8];
endmodule

// Registers
module RegisterFile (
  input  WriteEnable,
  input  [2:0] ReadRegister1,
  input  [2:0] ReadRegister2,
  input  [2:0] WriteRegister,
  input  [15:0] WriteData,
  input  Clock,
  input  Reset,
  output [15:0] ReadData2,
  output [15:0] ReadData1
);

  wire decoder_1_out0, decoder_1_out1, decoder_1_out2, decoder_1_out3, decoder_1_out4, decoder_1_out5,
       decoder_1_out6, decoder_1_out7;
  wire [15:0] demultiplexer_1_out0, demultiplexer_1_out1, demultiplexer_1_out2, demultiplexer_1_out3,
       demultiplexer_1_out4, demultiplexer_1_out5, demultiplexer_1_out6, demultiplexer_1_out7, Reg_0_q,
       Reg_1_q, Reg_2_q, Reg_3_q, Reg_4_q, Reg_5_q, Reg_6_q, Reg_7_q;

  Demultiplexer #(.select(3), .width(16), .enable("false")) demultiplexer_1 (
    .out0(demultiplexer_1_out0), .out1(demultiplexer_1_out1), .out2(demultiplexer_1_out2),
    .out3(demultiplexer_1_out3), .out4(demultiplexer_1_out4), .out5(demultiplexer_1_out5),
    .out6(demultiplexer_1_out6), .out7(demultiplexer_1_out7), .in(WriteData), .sel(WriteRegister));
  Decoder_part #(.select(3), .disabled(0)) decoder_1 (
    .out0(decoder_1_out0), .out1(decoder_1_out1), .out2(decoder_1_out2), .out3(decoder_1_out3),
    .out4(decoder_1_out4), .out5(decoder_1_out5), .out6(decoder_1_out6), .out7(decoder_1_out7),
    .sel(WriteRegister), .en(WriteEnable));
  Register #(.width(16)) Reg_0 (.D(demultiplexer_1_out0), .en(decoder_1_out0), .Q(Reg_0_q), .clk(Clock), .clr(Reset));
  Register #(.width(16)) Reg_1 (.D(demultiplexer_1_out1), .en(decoder_1_out1), .Q(Reg_1_q), .clk(Clock), .clr(Reset));
  Register #(.width(16)) Reg_2 (.D(demultiplexer_1_out2), .en(decoder_1_out2), .Q(Reg_2_q), .clk(Clock), .clr(Reset));
  Register #(.width(16)) Reg_3 (.D(demultiplexer_1_out3), .en(decoder_1_out3), .Q(Reg_3_q), .clk(Clock), .clr(Reset));
  Register #(.width(16)) Reg_4 (.D(demultiplexer_1_out4), .en(decoder_1_out4), .Q(Reg_4_q), .clk(Clock), .clr(Reset));
  Register #(.width(16)) Reg_5 (.D(demultiplexer_1_out5), .en(decoder_1_out5), .Q(Reg_5_q), .clk(Clock), .clr(Reset));
  Register #(.width(16)) Reg_6 (.D(demultiplexer_1_out6), .en(decoder_1_out6), .Q(Reg_6_q), .clk(Clock), .clr(Reset));
  Register #(.width(16)) Reg_7 (.D(demultiplexer_1_out7), .en(decoder_1_out7), .Q(Reg_7_q), .clk(Clock), .clr(Reset));
  Multiplexer #(.select(3), .width(16), .enable("false")) multiplexer_1 (
    .in0(Reg_0_q), .in1(Reg_1_q), .in2(Reg_2_q), .in3(Reg_3_q), .in4(Reg_4_q), .in5(Reg_5_q), .in6(Reg_6_q),
    .in7(Reg_7_q), .out(ReadData2), .sel(ReadRegister2));
  Multiplexer #(.select(3), .width(16), .enable("false")) multiplexer_2 (
    .in0(Reg_0_q), .in1(Reg_1_q), .in2(Reg_2_q), .in3(Reg_3_q), .in4(Reg_4_q), .in5(Reg_5_q), .in6(Reg_6_q),
    .in7(Reg_7_q), .out(ReadData1), .sel(ReadRegister1));
endmodule

module extender (
  input  Unsigned,
  input  [7:0] \input ,
  output [15:0] Result
);

  wire [15:0] bit_extender_1_out, bit_extender_2_out;

  assign bit_extender_1_out = {{8{\input [7]}}, \input };  // Bit_Extender bit_extender_1
  assign bit_extender_2_out = {{8{1'b0}}, \input };  // Bit_Extender bit_extender_2
  Multiplexer #(.width(16), .enable("false")) multiplexer_1 (
    .in0(bit_extender_1_out), .in1(bit_extender_2_out), .out(Result), .sel(Unsigned));
endmodule

module Shifter (
  input  right,
  input  amount,
  input  [15:0] Input,
  input  [15:0] Shift_Value,
  input  [3:0] ShAmt,
  output [15:0] Result
);

  wire [3:0] multiplexer_1_out;
  wire [15:0] shifter_1_out, shifter_2_out;

  Multiplexer #(.width(4), .enable("false")) multiplexer_1 (
    .in0(Shift_Value[4:1]), .in1(ShAmt), .out(multiplexer_1_out), .sel(amount));
  Shifter_part #(.width(16)) shifter_1 (.in(Input), .\dist (multiplexer_1_out), .out(shifter_1_out));
  Shifter_part #(.width(16), .shift("lr")) shifter_2 (.in(Input), .\dist (multiplexer_1_out), .out(shifter_2_out));
  Multiplexer #(.width(16), .enable("false")) multiplexer_2 (
    .in0(shifter_1_out), .in1(shifter_2_out), .out(Result), .sel(right));
endmodule

module ALUcontrol (
  input  [4:0] in_1,
  output [3:0] ALUOp
);

  wire and_2_out, and_3_out, not_1_out, not_2_out, not_3_out, not_4_out, not_5_out;

  not not_1 (not_1_out, in_1[4]);
  not not_2 (not_2_out, in_1[0]);
  not not_3 (not_3_out, in_1[1]);
  not not_4 (not_4_out, in_1[0]);
  not not_5 (not_5_out, in_1[2]);
  and and_1 (ALUOp[3], not_1_out, in_1[2], not_2_out);
  and and_2 (and_2_out, not_3_out, in_1[0]);
  and and_3 (and_3_out, in_1[2], not_4_out);
  or or_1 (ALUOp[1], not_5_out, in_1[4]);
  or or_2 (ALUOp[2], and_2_out, and_3_out, in_1[4]);

  assign ALUOp[0] = 1'b0;
endmodule

module RegOut (
  input  [4:0] in_1,
  output s
);

  wire and_1_out, and_2_out, and_3_out, and_4_out, not_1_out, not_2_out, not_3_out, not_4_out, not_5_out;

  not not_1 (not_1_out, in_1[3]);
  not not_2 (not_2_out, in_1[2]);
  and and_1 (and_1_out, not_1_out, not_2_out, in_1[1]);
  not not_3 (not_3_out, in_1[3]);
  and and_2 (and_2_out, not_3_out, in_1[2], not_4_out);
  not not_4 (not_4_out, in_1[1]);
  and and_3 (and_3_out, in_1[4], not_5_out);
  not not_5 (not_5_out, in_1[1]);
  and and_4 (and_4_out, in_1[4], in_1[2]);
  or or_1 (s, and_1_out, and_2_out, and_3_out, and_4_out);
endmodule

module MUXcontrol (
  input  [4:0] in_1,
  output [1:0] out_2
);

  wire and_1_out, and_2_out, not_1_out, not_2_out, not_3_out, not_4_out;

  not not_1 (not_1_out, in_1[3]);
  not not_2 (not_2_out, in_1[1]);
  not not_3 (not_3_out, in_1[2]);
  not not_4 (not_4_out, in_1[3]);
  and and_1 (and_1_out, not_1_out, in_1[2], not_2_out);
  and and_2 (and_2_out, in_1[3], not_3_out);
  or or_1 (out_2[0], not_4_out, in_1[4]);
  or or_2 (out_2[1], and_1_out, and_2_out);
endmodule

module Put_Control (
  input  [15:0] \input ,
  input  [4:0] opCode,
  input  Reset,
  output [3:0] Hex0,
  output [3:0] Hex1,
  output [3:0] Hex2,
  output [3:0] Hex3
);

  wire nand_1_out;

  Register #(.width(16)) register_1 (
    .D(\input ), .Q({Hex3, Hex2, Hex1, Hex0}), .clk(nand_1_out), .clr(Reset));  // open: en
  nand nand_1 (nand_1_out, opCode[1], opCode[2], opCode[3], opCode[4]);
endmodule

module Halt_Control (
  input  [4:0] in_1,
  output Halt
);

  wire not_1_out;

  not not_1 (not_1_out, in_1[4]);
  nand nand_1 (Halt, in_1[1], in_1[2], in_1[3], not_1_out);
endmodule

module Write_Control (
  input  [4:0] in_1,
  output write
);

  wire and_1_out, and_2_out, and_3_out, and_4_out, not_1_out, not_2_out, not_3_out, not_4_out, not_5_out,
       not_6_out, not_7_out, not_8_out, not_9_out;

  not not_1 (not_1_out, in_1[4]);
  not not_2 (not_2_out, in_1[3]);
  not not_3 (not_3_out, in_1[4]);
  not not_4 (not_4_out, in_1[2]);
  not not_5 (not_5_out, in_1[4]);
  not not_6 (not_6_out, in_1[1]);
  not not_7 (not_7_out, in_1[0]);
  not not_8 (not_8_out, in_1[2]);
  not not_9 (not_9_out, in_1[1]);
  and and_1 (and_1_out, not_1_out, not_2_out);
  and and_2 (and_2_out, not_3_out, not_4_out);
  and and_3 (and_3_out, not_5_out, not_6_out, not_7_out);
  and and_4 (and_4_out, in_1[3], not_8_out, not_9_out);
  or or_1 (write, and_1_out, and_2_out, and_3_out, and_4_out);
endmodule

module Load_Store (
  input  [4:0] in_1,
  output load
);

  wire not_1_out, not_2_out, not_3_out;

  not not_1 (not_1_out, in_1[3]);
  not not_2 (not_2_out, in_1[2]);
  not not_3 (not_3_out, in_1[0]);
  or or_1 (load, not_1_out, not_2_out, not_3_out, in_1[1], in_1[4]);
endmodule

module shift_control (
  input  [4:0] in_1,
  output amount,
  output right
);


  assign amount = in_1[1];
  assign right = in_1[0];
endmodule

module MUXControl (
  input  [4:0] in_1,
  output [1:0] out_2
);

  wire not_1_out, not_2_out;

  not not_1 (not_1_out, in_1[2]);
  not not_2 (not_2_out, in_1[3]);
  and and_1 (out_2[1], in_1[3], not_1_out);
  or or_1 (out_2[0], not_2_out, in_1[4]);
endmodule

module PC_control (
  input  [4:0] in_1,
  input  zero,
  input  negative,
  output first,
  output second
);

  wire and_1_out, and_2_out, and_3_out, and_4_out, and_5_out, not_1_out, not_2_out, not_3_out, not_4_out,
       not_5_out, not_6_out, not_7_out, not_8_out, not_9_out, not_10_out;

  not not_1 (not_1_out, in_1[2]);
  not not_2 (not_2_out, in_1[1]);
  not not_3 (not_3_out, in_1[2]);
  not not_4 (not_4_out, zero);
  not not_5 (not_5_out, in_1[1]);
  not not_6 (not_6_out, zero);
  not not_7 (not_7_out, negative);
  not not_8 (not_8_out, in_1[3]);
  not not_9 (not_9_out, in_1[1]);
  not not_10 (not_10_out, in_1[2]);
  and and_1 (and_1_out, in_1[4], not_1_out, not_2_out, zero);
  and and_2 (and_2_out, in_1[4], not_3_out, in_1[1], not_4_out);
  and and_3 (and_3_out, in_1[4], in_1[2], not_5_out, not_6_out, not_7_out);
  and and_4 (and_4_out, in_1[4], not_8_out, in_1[2], in_1[1], negative);
  and and_5 (and_5_out, in_1[4], in_1[3], not_9_out);
  and and_6 (second, in_1[4], in_1[3], not_10_out, in_1[1]);
  or or_1 (first, and_1_out, and_2_out, and_3_out, and_4_out, and_5_out);
endmodule

module Branch (
  input  [15:0] in_1,
  output Zero,
  output Negative
);

  nor nor_1 (Zero, in_1[0], in_1[1], in_1[2], in_1[3], in_1[4], in_1[5], in_1[6], in_1[7], in_1[9], in_1[10], in_1[11], in_1[12], in_1[13], in_1[14], in_1[15], in_1[8]);

  assign Negative = in_1[15];
endmodule
